// Logisim project scheme-v2.circ as structural Verilog: 12 circuits, main circuit ui
module main (
  input  bus_0,
  input  bus_0_2,
  input  bus_0_3,
  output gameOver,
  output [3:0] bus_0_4,
  output [3:0] bus_0_5,
  output [3:0] bus_0_6,
  output [3:0] bus_0_7,
  output [3:0] bus_0_8,
  output [3:0] bus_0_9
);

  wire and_3_out, and_4_out, and_5_out, and_8_out, and_9_out, and_10_out, and_11_out, and_13_out, and_15_out,
       back, buffer_1_out, buffer_2_out, cdm_8_mark5_1_data_inst, cdm_8_mark5_1_mem_cycle,
       cdm_8_mark5_1_stop, check, clk, comparator_2_gt, comparator_3_lt, csField, csFig, decoder_1_out0,
       decoder_1_out1, draw, field_1_full, getNew, IAck, IO, IOsel, IRQ, keyboard, not_1_out, not_2_out,
       or_2_out, r, READwrite, register_2_q, register_4_q, register_6_q, rotate, status, \union , w;
  wire [1:0] or_3_out;
  wire [2:0] vec;
  wire [7:0] addr, cdm_8_mark5_1_data_out, cdm_8_mark5_1_pc, cdm_8_mark5_1_ps, cdm_8_mark5_1_r0,
       cdm_8_mark5_1_r1, cdm_8_mark5_1_r2, cdm_8_mark5_1_r3, cdm_8_mark5_1_sp, controlled_buffer_2_out,
       counter_1_q, field_1_bus_0, field_1_bus_1, field_1_fail, figNext, in, IOdat, out, register_3_q,
       register_5_q, score_out, X, Y;
  wire [31:0] score, scoredisp_2_bus_0_3, scoredisp_3_bus_0_3, scoredisp_4_bus_0_3, scoredisp_5_bus_0_3,
       scoredisp_6_bus_0_3;
  wire [31:8] pull_resistor_2_node;

  Clock clock_1 (.out(clk));
  // Probe on cdm_8_mark5_1_r3
  // Probe on cdm_8_mark5_1_r2
  // Probe on cdm_8_mark5_1_r1
  // Probe on cdm_8_mark5_1_r0
  Comparator comparator_1 (.a(8'h54), .b(cdm_8_mark5_1_pc), .eq(gameOver));  // open: gt, lt
  // Probe on cdm_8_mark5_1_sp
  // Probe on cdm_8_mark5_1_pc
  // Probe on cdm_8_mark5_1_ps
  CdM_8_mark5 cdm_8_mark5_1 (
    .clock(clk), .addr(addr), .mem_read(READwrite), .mem_cycle(cdm_8_mark5_1_mem_cycle),
    .data_inst(cdm_8_mark5_1_data_inst), .data_out(cdm_8_mark5_1_data_out),
    .data_in(controlled_buffer_2_out), .r0(cdm_8_mark5_1_r0), .r1(cdm_8_mark5_1_r1), .r2(cdm_8_mark5_1_r2),
    .r3(cdm_8_mark5_1_r3), .PC(cdm_8_mark5_1_pc), .SP(cdm_8_mark5_1_sp), .PS(cdm_8_mark5_1_ps), .IAck(IAck),
    .IRQ(IRQ), .vec(vec), .stop(cdm_8_mark5_1_stop));
  and and_1 (IOsel, IO, decoder_1_out1);
  Decoder #(.disabled(0)) decoder_1 (
    .out0(decoder_1_out0), .out1(decoder_1_out1), .sel(cdm_8_mark5_1_data_inst), .en(cdm_8_mark5_1_mem_cycle));
  not not_1 (not_1_out, READwrite);
  assign IOdat = not_1_out ? cdm_8_mark5_1_data_out : 8'bz;  // Controlled_Buffer controlled_buffer_1
  assign controlled_buffer_2_out = READwrite ? IOdat : 8'bz;  // Controlled_Buffer controlled_buffer_2
  Comparator comparator_2 (.a(addr), .b(8'hef), .gt(comparator_2_gt));  // open: eq, lt
  and and_2 (IO, comparator_2_gt, comparator_3_lt);
  Comparator comparator_3 (.a(addr), .b(8'hf8), .lt(comparator_3_lt));  // open: gt, eq
  and and_3 (and_3_out, decoder_1_out1, ~IOsel);  // AND_Gate
  // Probe on cdm_8_mark5_1_stop
  // Probe on addr
  not not_2 (not_2_out, clk);
  // Probe on IOdat
  RAM ram_1 (.addr(addr), .data(IOdat), .sel(and_3_out), .clk(not_2_out), .ld(READwrite));  // open: clr
  ROM rom_1 (.addr(addr), .data(IOdat), .sel(decoder_1_out0));
  // Probe on in
  assign in = w ? IOdat : 8'bz;  // Controlled_Buffer controlled_buffer_3
  assign IOdat = and_4_out ? out : 8'bz;  // Controlled_Buffer controlled_buffer_4
  and and_4 (and_4_out, READwrite, r);
  Register register_1 (
    .D(IOdat), .en(and_5_out), .Q({back, draw, \union , check, rotate, getNew, csField, csFig}), .clk(clk));  // open: clr
  and and_5 (and_5_out, IOsel, ~addr[0], ~addr[1], ~addr[2], ~addr[3]);  // AND_Gate
  // Probe on out
  and and_6 (w, IOsel, addr[0], ~addr[1], ~addr[2], ~addr[3]);  // AND_Gate
  and and_7 (r, IOsel, ~addr[0], addr[1], ~addr[2], ~addr[3]);  // AND_Gate
  Counter counter_1 (.Q(counter_1_q), .clk(field_1_full), .clr(register_2_q));  // open: load, D, count, carry
  // Probe on field_1_bus_0
  // Probe on field_1_bus_1
  field field_1 (
    .cs(csField), .\input (in), .x(X), .y(Y), .w(w), .r(and_4_out), .check(check), .\union (\union ),
    .draw(draw), .bus_0(field_1_bus_0), .full(field_1_full), .bus_1(field_1_bus_1), .fail(field_1_fail[0]),
    .nextFigure(figNext));
  Pull_Resistor pull_resistor_1 (.node(field_1_fail));
  ioreg u_X (.in(IOdat), .addrEn(and_8_out), .rw(READwrite), .IOout(IOdat), .clk(clk), .out(X));
  and and_8 (and_8_out, IOsel, addr[0], addr[1], ~addr[2], ~addr[3]);  // AND_Gate
  Register #(.width(1), .trigger("falling")) register_2 (.D(and_9_out), .Q(register_2_q), .clk(clk));  // open: en, clr
  and and_9 (and_9_out, ~csField, ~csFig, r);  // AND_Gate
  tetris tetris_1 (.cs(csFig), .rotate(rotate), .getNew(getNew), .r(r), .back(back), .next(figNext), .out(out));
  Register #(.trigger("high")) register_3 (
    .D(field_1_fail), .Q(register_3_q), .clk(field_1_fail[0]), .clr(register_4_q));  // open: en
  assign IOdat = and_10_out ? register_3_q : 8'bz;  // Controlled_Buffer controlled_buffer_5
  and and_10 (and_10_out, READwrite, status);
  assign IOdat = and_9_out ? counter_1_q : 8'bz;  // Controlled_Buffer controlled_buffer_6
  Register #(.width(1), .trigger("falling")) register_4 (.D(and_10_out), .Q(register_4_q), .clk(clk));  // open: en, clr
  ioreg u_Y (.in(IOdat), .addrEn(and_11_out), .rw(READwrite), .IOout(IOdat), .clk(clk), .out(Y));
  and and_11 (and_11_out, IOsel, ~addr[0], ~addr[1], addr[2], ~addr[3]);  // AND_Gate
  scoreDisp scoredisp_1 (.bus_0(scoredisp_2_bus_0_3), .bus_0_2(bus_0_4));  // open: bus_0_3
  or or_1 (or_3_out[1], bus_0, bus_0_2);
  and and_12 (status, IOsel, addr[0], addr[1], addr[2], ~addr[3]);  // AND_Gate
  scoreDisp scoredisp_2 (.bus_0(scoredisp_3_bus_0_3), .bus_0_2(bus_0_5), .bus_0_3(scoredisp_2_bus_0_3));
  scoreDisp scoredisp_3 (.bus_0(scoredisp_5_bus_0_3), .bus_0_2(bus_0_6), .bus_0_3(scoredisp_3_bus_0_3));
  // _17x20_4_bit_LCD 17x20_4_bit_lcd_1: pin names not known
  or or_2 (or_2_out, or_3_out[1], or_3_out[0]);
  buf buffer_1 (buffer_1_out, or_2_out);
  or or_3 (or_3_out[0], bus_0_2, bus_0_3);
  and and_13 (and_13_out, READwrite, keyboard);
  and and_14 (keyboard, IOsel, ~addr[0], addr[1], addr[2], ~addr[3]);  // AND_Gate
  scoreDisp scoredisp_4 (.bus_0(scoredisp_6_bus_0_3), .bus_0_2(bus_0_8), .bus_0_3(scoredisp_4_bus_0_3));
  scoreDisp scoredisp_5 (.bus_0(scoredisp_4_bus_0_3), .bus_0_2(bus_0_7), .bus_0_3(scoredisp_5_bus_0_3));
  assign IOdat = and_13_out ? register_5_q : 8'bz;  // Controlled_Buffer controlled_buffer_7
  Register register_5 (
    .D({{6{1'b0}}, or_3_out}), .Q(register_5_q), .clk(buffer_2_out), .clr(register_6_q));  // open: en
  buf buffer_2 (buffer_2_out, buffer_1_out);
  Register #(.width(1), .trigger("falling")) register_6 (.D(and_13_out), .Q(register_6_q), .clk(clk));  // open: en, clr
  scoreDisp scoredisp_6 (.bus_0(score), .bus_0_2(bus_0_9), .bus_0_3(scoredisp_6_bus_0_3));
  ioreg u_score (.in(IOdat), .addrEn(and_15_out), .rw(READwrite), .IOout(IOdat), .clk(clk), .out(score_out));
  and and_15 (and_15_out, IOsel, addr[0], ~addr[1], addr[2], ~addr[3]);  // AND_Gate
  Pull_Resistor pull_resistor_2 (.node({pull_resistor_2_node, score_out}));
  Multiplier #(.width(32)) multiplier_1 (
    .a({pull_resistor_2_node, score_out}), .b(32'h64), .out(score));  // open: cin, cout

  // Other names for the same wires on the sheet: IOaddr[3:0] = addr[3:0]

  // Notes on the sheet:
  //   contents of rom_1 (hex, n*v repeats v):
  //   d6 3a d6 c1 d0 f6 b1 d2 0 79 e0 36 d2 3 76 e1 15 d6 cc ee 4 d0 f3 b2 d3 e9 ae d3 2 77 e1 23 8a ee 24
  //   8e a2 d6 58 f e0 30 d1 e9 b6 d0 f3 a2 d3 0 d6 c1 ee 4 d6 6d ee 4 d0 f0 d1 7 a1 d6 e0 d1 0 a1 d0 f3
  //   d1 3 a1 d0 f4 d1 0 a1 d6 58 f e0 54 d4 d1 0 a1 d7 d0 f0 d1 12 a1 d6 66 d1 0 a1 d1 f7 b7 d7 d1 f2
  //   4*b7 d7 d0 f4 b1 8d a1 d6 58 f e0 83 d0 f4 b1 89 a1 d6 86 d6 3a d0 f7 b3 d6 c1 d7 d0 f0 d1 62 a1 d1
  //   f2 8*b7 d1 0 a1 d0 f2 b2 a e0 c0 d1 f5 b4 d3 1 7e e1 aa d3 1 ee be d3 2 7e e1 b3 d3 3 ee be d3 3 7e
  //   e1 bc d3 7 ee be d3 f 1c a4 d7 d0 f0 d1 42 a1 d6 66 d1 0 a1 d7 d0 f0 d1 b a1 d6 e0 d6 58 f e0 dd d1
  //   87 a1 d6 e0 d6 c1 d7 d1 f1 d2 f2 bb a7 bb a7 d7 9*0 1 4*0 1
endmodule

module tetris (
  input  cs,
  input  rotate,
  input  getNew,
  input  r,
  input  back,
  output [7:0] next,
  output [7:0] out
);

  wire and_1_out, n, or_2_out, rom, rot;
  wire [0:0] counter_2_q;
  wire [1:0] rotNum, subtractor_1_out;
  wire [7:0] adder_2_out, controlled_buffer_1_out, figNum, figOffset, multiplier_2_out, random_1_out,
       rom_1_data, rotOffset;

  Random random_1 (.clk(n), .out(random_1_out));  // open: next, clr
  Subtractor #(.width(2)) subtractor_1 (.a(rotNum), .b(2'b01), .out(subtractor_1_out));  // open: bin, bout
  or or_1 (rot, back, and_1_out);
  and and_1 (and_1_out, rotate, cs);
  and and_2 (n, cs, ~back, getNew);  // AND_Gate
  Divider divider_1 (.a(random_1_out), .b(8'h7), .rem(next));  // open: out, upper
  // Probe on next
  Counter #(.width(2), .max('h3)) counter_1 (
    .load(back), .D(subtractor_1_out), .Q(rotNum), .clk(or_2_out), .clr(n));  // open: count, carry
  or or_2 (or_2_out, back, rot);
  or or_3 (rom, rot, n);
  Register register_1 (.D(next), .Q(figNum), .clk(n));  // open: en, clr
  Multiplier multiplier_1 (.a(figNum), .b(8'h8), .out(figOffset));  // open: cin, cout
  Adder adder_1 (.a(figOffset), .b(multiplier_2_out), .out(rotOffset));  // open: cin, cout
  Multiplier multiplier_2 (.a({{6{1'b0}}, rotNum}), .b(8'h2), .out(multiplier_2_out));  // open: cin, cout
  assign controlled_buffer_1_out = n ? figOffset : 8'bz;  // Controlled_Buffer controlled_buffer_1
  assign controlled_buffer_1_out = rot ? rotOffset : 8'bz;  // Controlled_Buffer controlled_buffer_2
  Counter #(.width(1), .max('h1), .trigger("falling")) counter_2 (
    .count(rom), .Q(counter_2_q[0]), .clk(r));  // open: load, D, carry, clr
  Adder adder_2 (.a(controlled_buffer_1_out), .b({{7{1'b0}}, counter_2_q[0]}), .out(adder_2_out));  // open: cin, cout
  ROM rom_1 (.addr(adder_2_out), .data(rom_1_data), .sel(rom));
  assign out = rom ? rom_1_data : 8'bz;  // Controlled_Buffer controlled_buffer_3

  // Other names for the same wires on the sheet: figNextNum[7:0] = next

  // Notes on the sheet:
  //   contents of rom_1 (hex, n*v repeats v):
  //   f 0 22 22 0 f0 44 44 8e 0 64 40 e 20 44 c0 2e 0 44 60 e 80 c4 40 66 0 66 0 66 0 66 0 6c 0 46 20 6 c0
  //   8c 40 4e 0 46 40 e 40 4c 40 c6 0 26 40 c 60 4c 80
endmodule

module _4to32 (
  input  [3:0] in,
  input  [7:0] x,
  output [31:0] bus_0,
  output fail
);

  wire comparator_1_lt, comparator_2_gt, comparator_2_lt, or_1_out;
  wire [31:0] and_1_out;

  Shifter #(.width(32), .shift("lr")) shifter_1 (.in({in, {28{1'b0}}}), .\dist (x[4:0]), .out(bus_0));
  assign and_1_out = bus_0 & 32'hfff;  // AND_Gate and_1, 32 bits wide
  Comparator comparator_1 (.a(x), .b({8{1'b0}}), .lt(comparator_1_lt));  // open: gt, eq
  Comparator #(.width(32)) comparator_2 (
    .a(and_1_out), .b({32{1'b0}}), .gt(comparator_2_gt), .lt(comparator_2_lt));  // open: eq
  or or_1 (or_1_out, comparator_2_gt, comparator_2_lt);
  or or_2 (fail, or_1_out, comparator_1_lt);
endmodule

module field (
  input  cs,
  input  [7:0] \input ,
  input  [7:0] x,
  input  [7:0] y,
  input  w,
  input  r,
  input  check,
  input  \union ,
  input  draw,
  input  [7:0] nextFigure,
  output [7:0] bus_0,
  output full,
  output [7:0] bus_1,
  output fail
);

  wire and_1_out, and_2_out, and_3_out, and_5_out, buffer_1_out, buffer_2_out, buffer_3_out, clk,
       comparator_1_gt, comparator_2_eq, comparator_3_eq, fail_t, fieldcell_1_checkout, fieldcell_1_clkout,
       fieldcell_1_unionout, fieldcell_2_checkout, fieldcell_2_clkout, fieldcell_2_unionout,
       fieldcell_3_checkout, fieldcell_3_clkout, fieldcell_3_unionout, fieldcell_4_checkout,
       fieldcell_4_clkout, fieldcell_4_unionout, fieldcell_5_checkout, fieldcell_5_clkout,
       fieldcell_5_unionout, fieldcell_6_checkout, fieldcell_6_clkout, fieldcell_6_unionout,
       fieldcell_7_checkout, fieldcell_7_clkout, fieldcell_7_unionout, fieldcell_8_checkout,
       fieldcell_8_clkout, fieldcell_8_unionout, fieldcell_9_checkout, fieldcell_9_clkout,
       fieldcell_9_unionout, fieldcell_10_checkout, fieldcell_10_clkout, fieldcell_10_unionout,
       fieldcell_11_checkout, fieldcell_11_clkout, fieldcell_11_unionout, fieldcell_12_checkout,
       fieldcell_12_clkout, fieldcell_12_unionout, fieldcell_13_checkout, fieldcell_13_clkout,
       fieldcell_13_unionout, fieldcell_14_checkout, fieldcell_14_clkout, fieldcell_14_unionout,
       fieldcell_15_checkout, fieldcell_15_clkout, fieldcell_15_unionout, fieldcell_16_checkout,
       fieldcell_16_clkout, fieldcell_16_unionout, fieldcell_17_checkout, fieldcell_17_clkout,
       fieldcell_17_unionout, fieldcell_18_checkout, fieldcell_18_clkout, fieldcell_18_unionout,
       fieldcell_19_checkout, fieldcell_19_clkout, fieldcell_19_unionout, fieldcell_20_unionout, not_1_out,
       not_3_out, or_1_out, or_2_out, pull_resistor_2_node, r_t, w_t;
  wire [0:0] controlled_buffer_1_out;
  wire [1:0] counter, counter_2_q;
  wire [2:0] counter_1_q;
  wire [3:0] multiplexer_1_out;
  wire [4:0] adder_1_out, adder_3_out, fieldcell_1_idnext, fieldcell_1_yout, fieldcell_2_idnext,
       fieldcell_2_yout, fieldcell_3_idnext, fieldcell_3_yout, fieldcell_4_idnext, fieldcell_4_yout,
       fieldcell_5_idnext, fieldcell_5_yout, fieldcell_6_idnext, fieldcell_6_yout, fieldcell_7_idnext,
       fieldcell_7_yout, fieldcell_8_idnext, fieldcell_8_yout, fieldcell_9_idnext, fieldcell_9_yout,
       fieldcell_10_idnext, fieldcell_10_yout, fieldcell_11_idnext, fieldcell_11_yout, fieldcell_12_idnext,
       fieldcell_12_yout, fieldcell_13_idnext, fieldcell_13_yout, fieldcell_14_idnext, fieldcell_14_yout,
       fieldcell_15_idnext, fieldcell_15_yout, fieldcell_16_idnext, fieldcell_16_yout, fieldcell_17_idnext,
       fieldcell_17_yout, fieldcell_18_idnext, fieldcell_18_yout, fieldcell_19_idnext, fieldcell_19_yout,
       fieldcell_20_idnext, yIt;
  wire [7:5] pull_resistor_3_node;
  wire [31:0] and_4_out, checkRow, clr, fieldcell_1_clrout, fieldcell_1_lastout, fieldcell_1_xout,
       fieldcell_2_clrout, fieldcell_2_lastout, fieldcell_2_xout, fieldcell_3_clrout, fieldcell_3_lastout,
       fieldcell_3_xout, fieldcell_4_clrout, fieldcell_4_lastout, fieldcell_4_xout, fieldcell_5_clrout,
       fieldcell_5_lastout, fieldcell_5_xout, fieldcell_6_clrout, fieldcell_6_lastout, fieldcell_6_xout,
       fieldcell_7_clrout, fieldcell_7_lastout, fieldcell_7_xout, fieldcell_8_clrout, fieldcell_8_lastout,
       fieldcell_8_xout, fieldcell_9_clrout, fieldcell_9_lastout, fieldcell_9_xout, fieldcell_10_clrout,
       fieldcell_10_lastout, fieldcell_10_xout, fieldcell_11_clrout, fieldcell_11_lastout, fieldcell_11_xout,
       fieldcell_12_clrout, fieldcell_12_lastout, fieldcell_12_xout, fieldcell_13_clrout,
       fieldcell_13_lastout, fieldcell_13_xout, fieldcell_14_clrout, fieldcell_14_lastout, fieldcell_14_xout,
       fieldcell_15_clrout, fieldcell_15_lastout, fieldcell_15_xout, fieldcell_16_clrout,
       fieldcell_16_lastout, fieldcell_16_xout, fieldcell_17_clrout, fieldcell_17_lastout, fieldcell_17_xout,
       fieldcell_18_clrout, fieldcell_18_lastout, fieldcell_18_xout, fieldcell_19_clrout,
       fieldcell_19_lastout, fieldcell_19_xout, fieldcell_20_lastout, n17x20_4_bit_lcd_1_p21,
       n17x20_4_bit_lcd_1_p22, n17x20_4_bit_lcd_1_p23, n17x20_4_bit_lcd_1_p24, n17x20_4_bit_lcd_1_p25,
       n17x20_4_bit_lcd_1_p26, n17x20_4_bit_lcd_1_p27, n17x20_4_bit_lcd_1_p28, n17x20_4_bit_lcd_1_p29,
       n17x20_4_bit_lcd_1_p30, n17x20_4_bit_lcd_1_p31, n17x20_4_bit_lcd_1_p32, n17x20_4_bit_lcd_1_p33,
       n17x20_4_bit_lcd_1_p34, n17x20_4_bit_lcd_1_p35, n17x20_4_bit_lcd_1_p36, n17x20_4_bit_lcd_1_p37,
       n17x20_4_bit_lcd_1_p38, n17x20_4_bit_lcd_1_p39, n17x20_4_bit_lcd_1_p40, register_1_q, shifter_3_out,
       xRow;

  buf buffer_1 (buffer_1_out, buffer_3_out);
  buf buffer_2 (buffer_2_out, w);
  buf buffer_3 (buffer_3_out, buffer_2_out);
  assign {counter, controlled_buffer_1_out[0]} = \union  ? counter_1_q : 3'bz;  // Controlled_Buffer controlled_buffer_1
  Counter #(.width(3), .max('h7), .trigger("falling")) counter_1 (
    .count(cs), .Q(counter_1_q), .clk(and_1_out));  // open: load, D, carry, clr
  and and_1 (and_1_out, \union , r_t);
  Shift_Register #(.width(8), .length(2)) shift_register_1 (
    .shift(cs), .in(\input ), .clk(w_t), .q0(bus_1), .q1(bus_0));  // open: out, load, clr, d0, d1
  buf buffer_4 (w_t, buffer_1_out);
  Pull_Resistor pull_resistor_1 (.node(r_t));
  assign r_t = and_2_out ? r : 1'bz;  // Controlled_Buffer controlled_buffer_2
  and and_2 (and_2_out, or_1_out, cs);
  or or_1 (or_1_out, check, \union , draw);
  Pull_Resistor pull_resistor_2 (.node(pull_resistor_2_node));
  assign counter = not_1_out ? counter_2_q : 2'bz;  // Controlled_Buffer controlled_buffer_3
  Counter #(.width(2), .max('h3), .trigger("falling")) counter_2 (
    .count(cs), .Q(counter_2_q), .clk(and_3_out));  // open: load, D, carry, clr
  not not_1 (not_1_out, \union );
  and and_3 (and_3_out, ~\union , r_t);  // AND_Gate
  Pull_Resistor pull_resistor_3 (.node({pull_resistor_3_node, yIt}));
  Multiplexer #(.select(2), .width(4), .enable("false")) multiplexer_1 (
    .in0(bus_0[7:4]), .in1(bus_0[3:0]), .in2(bus_1[7:4]), .in3(bus_1[3:0]), .out(multiplexer_1_out),
    .sel(counter));
  // Probe on {3'b000, counter}
  Comparator #(.mode("unsigned")) comparator_1 (
    .a({pull_resistor_3_node, yIt}), .b(8'h13), .gt(comparator_1_gt));  // open: eq, lt
  Comparator #(.width(32)) comparator_2 (.a(xRow), .b({32{1'b0}}), .eq(comparator_2_eq));  // open: gt, lt
  Shifter #(.width(32), .shift("lr")) shifter_1 (
    .in({multiplexer_1_out, {28{1'b0}}}), .\dist (adder_1_out), .out(checkRow));
  Adder #(.width(5)) adder_1 (.a(x[4:0]), .b(5'b00100), .out(adder_1_out));  // open: cin, cout
  Adder #(.width(5)) adder_2 (.a({3'b000, counter}), .b(y[4:0]), .out(yIt));  // open: cin, cout
  assign fail_t = comparator_1_gt ? ~comparator_2_eq : 1'bz;  // Controlled_Inverter controlled_inverter_1
  Shifter #(.width(32)) shifter_2 (.in(checkRow), .\dist (5'b00100), .out(xRow));
  Adder #(.width(5)) adder_3 (.a(yIt), .b(5'b00001), .out(adder_3_out));  // open: cin, cout
  assign and_4_out = 32'hffc0000 & checkRow;  // AND_Gate and_4, 32 bits wide
  assign clr = ~shifter_3_out;  // NOT_Gate not_2, 32 bits wide
  Shifter #(.width(32), .shift("lr")) shifter_3 (.in({32{1'b1}}), .\dist (adder_3_out), .out(shifter_3_out));
  not not_3 (not_3_out, comparator_3_eq);
  Comparator #(.width(32)) comparator_3 (.a(and_4_out), .b(checkRow), .eq(comparator_3_eq));  // open: gt, lt
  eq eq_1 (.A(register_1_q), .B(32'hffc00000));  // open: r
  Register #(.width(32)) register_1 (.Q(register_1_q), .clk(clk));  // open: D, en, clr
  or or_2 (or_2_out, fail_t, not_3_out);
  assign fail = r_t ? or_2_out : 1'bz;  // Controlled_Buffer controlled_buffer_4
  fieldCell fieldcell_1 (
    .xRow(xRow), .y(yIt), .id({5{1'b0}}), .clrMap(clr), .lastIn({32{1'b0}}), .clk(r_t), .check(check),
    .\union (\union ), .full(full), .xOut(fieldcell_1_xout), .full_2(full), .yOut(fieldcell_1_yout),
    .idNext(fieldcell_1_idnext), .fail(fail_t), .clrOut(fieldcell_1_clrout), .lastOut(fieldcell_1_lastout),
    .clkOut(fieldcell_1_clkout), .checkOut(fieldcell_1_checkout), .unionOut(fieldcell_1_unionout));
  fieldCell fieldcell_2 (
    .xRow(fieldcell_1_xout), .y(fieldcell_1_yout), .id(fieldcell_1_idnext), .clrMap(fieldcell_1_clrout),
    .lastIn(fieldcell_1_lastout), .clk(fieldcell_1_clkout), .check(fieldcell_1_checkout),
    .\union (fieldcell_1_unionout), .full(full), .xOut(fieldcell_2_xout), .full_2(full),
    .yOut(fieldcell_2_yout), .idNext(fieldcell_2_idnext), .fail(fail_t), .clrOut(fieldcell_2_clrout),
    .lastOut(fieldcell_2_lastout), .clkOut(fieldcell_2_clkout), .checkOut(fieldcell_2_checkout),
    .unionOut(fieldcell_2_unionout));
  fieldCell fieldcell_3 (
    .xRow(fieldcell_2_xout), .y(fieldcell_2_yout), .id(fieldcell_2_idnext), .clrMap(fieldcell_2_clrout),
    .lastIn(fieldcell_2_lastout), .clk(fieldcell_2_clkout), .check(fieldcell_2_checkout),
    .\union (fieldcell_2_unionout), .full(full), .xOut(fieldcell_3_xout), .full_2(full),
    .yOut(fieldcell_3_yout), .idNext(fieldcell_3_idnext), .fail(fail_t), .clrOut(fieldcell_3_clrout),
    .lastOut(fieldcell_3_lastout), .clkOut(fieldcell_3_clkout), .checkOut(fieldcell_3_checkout),
    .unionOut(fieldcell_3_unionout));
  fieldCell fieldcell_4 (
    .xRow(fieldcell_3_xout), .y(fieldcell_3_yout), .id(fieldcell_3_idnext), .clrMap(fieldcell_3_clrout),
    .lastIn(fieldcell_3_lastout), .clk(fieldcell_3_clkout), .check(fieldcell_3_checkout),
    .\union (fieldcell_3_unionout), .full(full), .xOut(fieldcell_4_xout), .full_2(full),
    .yOut(fieldcell_4_yout), .idNext(fieldcell_4_idnext), .fail(fail_t), .clrOut(fieldcell_4_clrout),
    .lastOut(fieldcell_4_lastout), .clkOut(fieldcell_4_clkout), .checkOut(fieldcell_4_checkout),
    .unionOut(fieldcell_4_unionout));
  fieldCell fieldcell_5 (
    .xRow(fieldcell_4_xout), .y(fieldcell_4_yout), .id(fieldcell_4_idnext), .clrMap(fieldcell_4_clrout),
    .lastIn(fieldcell_4_lastout), .clk(fieldcell_4_clkout), .check(fieldcell_4_checkout),
    .\union (fieldcell_4_unionout), .full(full), .xOut(fieldcell_5_xout), .full_2(full),
    .yOut(fieldcell_5_yout), .idNext(fieldcell_5_idnext), .fail(fail_t), .clrOut(fieldcell_5_clrout),
    .lastOut(fieldcell_5_lastout), .clkOut(fieldcell_5_clkout), .checkOut(fieldcell_5_checkout),
    .unionOut(fieldcell_5_unionout));
  fieldCell fieldcell_6 (
    .xRow(fieldcell_5_xout), .y(fieldcell_5_yout), .id(fieldcell_5_idnext), .clrMap(fieldcell_5_clrout),
    .lastIn(fieldcell_5_lastout), .clk(fieldcell_5_clkout), .check(fieldcell_5_checkout),
    .\union (fieldcell_5_unionout), .full(full), .xOut(fieldcell_6_xout), .full_2(full),
    .yOut(fieldcell_6_yout), .idNext(fieldcell_6_idnext), .fail(fail_t), .clrOut(fieldcell_6_clrout),
    .lastOut(fieldcell_6_lastout), .clkOut(fieldcell_6_clkout), .checkOut(fieldcell_6_checkout),
    .unionOut(fieldcell_6_unionout));
  fieldCell fieldcell_7 (
    .xRow(fieldcell_6_xout), .y(fieldcell_6_yout), .id(fieldcell_6_idnext), .clrMap(fieldcell_6_clrout),
    .lastIn(fieldcell_6_lastout), .clk(fieldcell_6_clkout), .check(fieldcell_6_checkout),
    .\union (fieldcell_6_unionout), .full(full), .xOut(fieldcell_7_xout), .full_2(full),
    .yOut(fieldcell_7_yout), .idNext(fieldcell_7_idnext), .fail(fail_t), .clrOut(fieldcell_7_clrout),
    .lastOut(fieldcell_7_lastout), .clkOut(fieldcell_7_clkout), .checkOut(fieldcell_7_checkout),
    .unionOut(fieldcell_7_unionout));
  fieldCell fieldcell_8 (
    .xRow(fieldcell_7_xout), .y(fieldcell_7_yout), .id(fieldcell_7_idnext), .clrMap(fieldcell_7_clrout),
    .lastIn(fieldcell_7_lastout), .clk(fieldcell_7_clkout), .check(fieldcell_7_checkout),
    .\union (fieldcell_7_unionout), .full(full), .xOut(fieldcell_8_xout), .full_2(full),
    .yOut(fieldcell_8_yout), .idNext(fieldcell_8_idnext), .fail(fail_t), .clrOut(fieldcell_8_clrout),
    .lastOut(fieldcell_8_lastout), .clkOut(fieldcell_8_clkout), .checkOut(fieldcell_8_checkout),
    .unionOut(fieldcell_8_unionout));
  fieldCell fieldcell_9 (
    .xRow(fieldcell_8_xout), .y(fieldcell_8_yout), .id(fieldcell_8_idnext), .clrMap(fieldcell_8_clrout),
    .lastIn(fieldcell_8_lastout), .clk(fieldcell_8_clkout), .check(fieldcell_8_checkout),
    .\union (fieldcell_8_unionout), .full(full), .xOut(fieldcell_9_xout), .full_2(full),
    .yOut(fieldcell_9_yout), .idNext(fieldcell_9_idnext), .fail(fail_t), .clrOut(fieldcell_9_clrout),
    .lastOut(fieldcell_9_lastout), .clkOut(fieldcell_9_clkout), .checkOut(fieldcell_9_checkout),
    .unionOut(fieldcell_9_unionout));
  fieldCell fieldcell_10 (
    .xRow(fieldcell_9_xout), .y(fieldcell_9_yout), .id(fieldcell_9_idnext), .clrMap(fieldcell_9_clrout),
    .lastIn(fieldcell_9_lastout), .clk(fieldcell_9_clkout), .check(fieldcell_9_checkout),
    .\union (fieldcell_9_unionout), .full(full), .xOut(fieldcell_10_xout), .full_2(full),
    .yOut(fieldcell_10_yout), .idNext(fieldcell_10_idnext), .fail(fail_t), .clrOut(fieldcell_10_clrout),
    .lastOut(fieldcell_10_lastout), .clkOut(fieldcell_10_clkout), .checkOut(fieldcell_10_checkout),
    .unionOut(fieldcell_10_unionout));
  fieldCell fieldcell_11 (
    .xRow(fieldcell_10_xout), .y(fieldcell_10_yout), .id(fieldcell_10_idnext), .clrMap(fieldcell_10_clrout),
    .lastIn(fieldcell_10_lastout), .clk(fieldcell_10_clkout), .check(fieldcell_10_checkout),
    .\union (fieldcell_10_unionout), .full(full), .xOut(fieldcell_11_xout), .full_2(full),
    .yOut(fieldcell_11_yout), .idNext(fieldcell_11_idnext), .fail(fail_t), .clrOut(fieldcell_11_clrout),
    .lastOut(fieldcell_11_lastout), .clkOut(fieldcell_11_clkout), .checkOut(fieldcell_11_checkout),
    .unionOut(fieldcell_11_unionout));
  fieldCell fieldcell_12 (
    .xRow(fieldcell_11_xout), .y(fieldcell_11_yout), .id(fieldcell_11_idnext), .clrMap(fieldcell_11_clrout),
    .lastIn(fieldcell_11_lastout), .clk(fieldcell_11_clkout), .check(fieldcell_11_checkout),
    .\union (fieldcell_11_unionout), .full(full), .xOut(fieldcell_12_xout), .full_2(full),
    .yOut(fieldcell_12_yout), .idNext(fieldcell_12_idnext), .fail(fail_t), .clrOut(fieldcell_12_clrout),
    .lastOut(fieldcell_12_lastout), .clkOut(fieldcell_12_clkout), .checkOut(fieldcell_12_checkout),
    .unionOut(fieldcell_12_unionout));
  fieldCell fieldcell_13 (
    .xRow(fieldcell_12_xout), .y(fieldcell_12_yout), .id(fieldcell_12_idnext), .clrMap(fieldcell_12_clrout),
    .lastIn(fieldcell_12_lastout), .clk(fieldcell_12_clkout), .check(fieldcell_12_checkout),
    .\union (fieldcell_12_unionout), .full(full), .xOut(fieldcell_13_xout), .full_2(full),
    .yOut(fieldcell_13_yout), .idNext(fieldcell_13_idnext), .fail(fail_t), .clrOut(fieldcell_13_clrout),
    .lastOut(fieldcell_13_lastout), .clkOut(fieldcell_13_clkout), .checkOut(fieldcell_13_checkout),
    .unionOut(fieldcell_13_unionout));
  fieldCell fieldcell_14 (
    .xRow(fieldcell_13_xout), .y(fieldcell_13_yout), .id(fieldcell_13_idnext), .clrMap(fieldcell_13_clrout),
    .lastIn(fieldcell_13_lastout), .clk(fieldcell_13_clkout), .check(fieldcell_13_checkout),
    .\union (fieldcell_13_unionout), .full(full), .xOut(fieldcell_14_xout), .full_2(full),
    .yOut(fieldcell_14_yout), .idNext(fieldcell_14_idnext), .fail(fail_t), .clrOut(fieldcell_14_clrout),
    .lastOut(fieldcell_14_lastout), .clkOut(fieldcell_14_clkout), .checkOut(fieldcell_14_checkout),
    .unionOut(fieldcell_14_unionout));
  fieldCell fieldcell_15 (
    .xRow(fieldcell_14_xout), .y(fieldcell_14_yout), .id(fieldcell_14_idnext), .clrMap(fieldcell_14_clrout),
    .lastIn(fieldcell_14_lastout), .clk(fieldcell_14_clkout), .check(fieldcell_14_checkout),
    .\union (fieldcell_14_unionout), .full(full), .xOut(fieldcell_15_xout), .full_2(full),
    .yOut(fieldcell_15_yout), .idNext(fieldcell_15_idnext), .fail(fail_t), .clrOut(fieldcell_15_clrout),
    .lastOut(fieldcell_15_lastout), .clkOut(fieldcell_15_clkout), .checkOut(fieldcell_15_checkout),
    .unionOut(fieldcell_15_unionout));
  fieldCell fieldcell_16 (
    .xRow(fieldcell_15_xout), .y(fieldcell_15_yout), .id(fieldcell_15_idnext), .clrMap(fieldcell_15_clrout),
    .lastIn(fieldcell_15_lastout), .clk(fieldcell_15_clkout), .check(fieldcell_15_checkout),
    .\union (fieldcell_15_unionout), .full(full), .xOut(fieldcell_16_xout), .full_2(full),
    .yOut(fieldcell_16_yout), .idNext(fieldcell_16_idnext), .fail(fail_t), .clrOut(fieldcell_16_clrout),
    .lastOut(fieldcell_16_lastout), .clkOut(fieldcell_16_clkout), .checkOut(fieldcell_16_checkout),
    .unionOut(fieldcell_16_unionout));
  fieldCell fieldcell_17 (
    .xRow(fieldcell_16_xout), .y(fieldcell_16_yout), .id(fieldcell_16_idnext), .clrMap(fieldcell_16_clrout),
    .lastIn(fieldcell_16_lastout), .clk(fieldcell_16_clkout), .check(fieldcell_16_checkout),
    .\union (fieldcell_16_unionout), .full(full), .xOut(fieldcell_17_xout), .full_2(full),
    .yOut(fieldcell_17_yout), .idNext(fieldcell_17_idnext), .fail(fail_t), .clrOut(fieldcell_17_clrout),
    .lastOut(fieldcell_17_lastout), .clkOut(fieldcell_17_clkout), .checkOut(fieldcell_17_checkout),
    .unionOut(fieldcell_17_unionout));
  fieldCell fieldcell_18 (
    .xRow(fieldcell_17_xout), .y(fieldcell_17_yout), .id(fieldcell_17_idnext), .clrMap(fieldcell_17_clrout),
    .lastIn(fieldcell_17_lastout), .clk(fieldcell_17_clkout), .check(fieldcell_17_checkout),
    .\union (fieldcell_17_unionout), .full(full), .xOut(fieldcell_18_xout), .full_2(full),
    .yOut(fieldcell_18_yout), .idNext(fieldcell_18_idnext), .fail(fail_t), .clrOut(fieldcell_18_clrout),
    .lastOut(fieldcell_18_lastout), .clkOut(fieldcell_18_clkout), .checkOut(fieldcell_18_checkout),
    .unionOut(fieldcell_18_unionout));
  fieldCell fieldcell_19 (
    .xRow(fieldcell_18_xout), .y(fieldcell_18_yout), .id(fieldcell_18_idnext), .clrMap(fieldcell_18_clrout),
    .lastIn(fieldcell_18_lastout), .clk(fieldcell_18_clkout), .check(fieldcell_18_checkout),
    .\union (fieldcell_18_unionout), .full(full), .xOut(fieldcell_19_xout), .full_2(full),
    .yOut(fieldcell_19_yout), .idNext(fieldcell_19_idnext), .fail(fail_t), .clrOut(fieldcell_19_clrout),
    .lastOut(fieldcell_19_lastout), .clkOut(fieldcell_19_clkout), .checkOut(fieldcell_19_checkout),
    .unionOut(fieldcell_19_unionout));
  fieldCell fieldcell_20 (
    .xRow(fieldcell_19_xout), .y(fieldcell_19_yout), .id(fieldcell_19_idnext), .clrMap(fieldcell_19_clrout),
    .lastIn(fieldcell_19_lastout), .clk(fieldcell_19_clkout), .check(fieldcell_19_checkout),
    .\union (fieldcell_19_unionout), .full(full), .full_2(full), .idNext(fieldcell_20_idnext), .fail(fail_t),
    .lastOut(fieldcell_20_lastout), .unionOut(fieldcell_20_unionout));  // open: xOut, yOut, clrOut, clkOut, checkOut
  // Probe on fieldcell_20_idnext
  // _17x20_4_bit_LCD 17x20_4_bit_lcd_1: pin names not known; wires that end beside it: fieldcell_1_lastout, fieldcell_2_lastout, fieldcell_3_lastout, fieldcell_4_lastout, fieldcell_5_lastout, fieldcell_6_lastout, fieldcell_7_lastout, fieldcell_8_lastout, fieldcell_9_lastout, fieldcell_10_lastout, fieldcell_11_lastout, fieldcell_12_lastout, fieldcell_13_lastout, fieldcell_14_lastout, fieldcell_15_lastout, fieldcell_16_lastout, fieldcell_17_lastout, fieldcell_18_lastout, fieldcell_19_lastout, fieldcell_20_lastout, n17x20_4_bit_lcd_1_p21, n17x20_4_bit_lcd_1_p22, n17x20_4_bit_lcd_1_p23, n17x20_4_bit_lcd_1_p24, n17x20_4_bit_lcd_1_p25, n17x20_4_bit_lcd_1_p26, n17x20_4_bit_lcd_1_p27, n17x20_4_bit_lcd_1_p28, n17x20_4_bit_lcd_1_p29, n17x20_4_bit_lcd_1_p30, n17x20_4_bit_lcd_1_p31, n17x20_4_bit_lcd_1_p32, n17x20_4_bit_lcd_1_p33, n17x20_4_bit_lcd_1_p34, n17x20_4_bit_lcd_1_p35, n17x20_4_bit_lcd_1_p36, n17x20_4_bit_lcd_1_p37, n17x20_4_bit_lcd_1_p38, n17x20_4_bit_lcd_1_p39, n17x20_4_bit_lcd_1_p40
  drawCell drawcell_1 (
    .x(xRow), .y(y[4:0]), .yIt({3'b000, counter}), .clk(r_t), ._0(n17x20_4_bit_lcd_1_p21),
    ._0_4(n17x20_4_bit_lcd_1_p22), ._0_20(n17x20_4_bit_lcd_1_p32), ._0_7(n17x20_4_bit_lcd_1_p23),
    ._0_2(n17x20_4_bit_lcd_1_p33), ._0_10(n17x20_4_bit_lcd_1_p24), ._0_5(n17x20_4_bit_lcd_1_p34),
    ._0_13(n17x20_4_bit_lcd_1_p25), ._0_8(n17x20_4_bit_lcd_1_p35), ._0_3(n17x20_4_bit_lcd_1_p26),
    ._0_11(n17x20_4_bit_lcd_1_p36), ._0_6(n17x20_4_bit_lcd_1_p27), ._0_12(n17x20_4_bit_lcd_1_p37),
    ._0_9(n17x20_4_bit_lcd_1_p28), ._0_15(n17x20_4_bit_lcd_1_p38), ._0_14(n17x20_4_bit_lcd_1_p29),
    ._0_17(n17x20_4_bit_lcd_1_p39), ._0_16(n17x20_4_bit_lcd_1_p30), ._0_19(n17x20_4_bit_lcd_1_p40),
    .cs(draw), .nextFigure(nextFigure), .w(and_5_out), ._0_18(n17x20_4_bit_lcd_1_p31));
  and and_5 (and_5_out, cs, w_t);

  // Other names for the same wires on the sheet: x_t[4:0] = x[4:0]; y_t[4:0] = y[4:0]
endmodule

module eq (
  input  [31:0] A,
  input  [31:0] B,
  output r
);

  Comparator #(.width(32)) comparator_1 (.a(A), .b(B), .eq(r));  // open: gt, lt
endmodule

module fieldCell (
  input  [31:0] xRow,
  input  [4:0] y,
  input  [4:0] id,
  input  [31:0] clrMap,
  input  [31:0] lastIn,
  input  clk,
  input  check,
  input  \union ,
  input  full,
  output [31:0] xOut,
  output full_2,
  output [4:0] yOut,
  output [4:0] idNext,
  output fail,
  output [31:0] clrOut,
  output [31:0] lastOut,
  output clkOut,
  output checkOut,
  output unionOut
);

  wire and_2_out, and_3_out, and_4_out, and_5_out, and_7_out, comparator_1_gt, cs, eq_1_r, eq_2_r, eq_3_r,
       not_1_out, not_2_out, not_3_out, or_1_out, or_2_out;
  wire [31:0] and_1_out, and_6_out, controlled_buffer_1_out, or_3_out, shifter_1_out, xor_1_out;

  Comparator #(.width(5)) comparator_1 (.a(y), .b(id), .gt(comparator_1_gt), .eq(cs));  // open: lt
  or or_1 (or_1_out, cs, comparator_1_gt);
  assign and_1_out = clrMap & shifter_1_out;  // AND_Gate and_1, 32 bits wide
  Shifter #(.width(32), .shift("lr")) shifter_1 (.in(32'h80000000), .\dist (y), .out(shifter_1_out));
  and and_2 (and_2_out, or_1_out, \union , full);
  and and_3 (and_3_out, cs, \union );
  not not_1 (not_1_out, eq_1_r);
  eq eq_1 (.A(and_1_out), .B({32{1'b0}}), .r(eq_1_r));
  or or_2 (or_2_out, and_2_out, and_3_out);
  assign or_3_out = xRow | lastOut;  // OR_Gate or_3, 32 bits wide
  and and_4 (and_4_out, not_1_out, full);
  not not_2 (not_2_out, full);
  assign controlled_buffer_1_out = not_2_out ? or_3_out : 32'bz;  // Controlled_Buffer controlled_buffer_1
  assign controlled_buffer_1_out = and_4_out ? lastIn : 32'bz;  // Controlled_Buffer controlled_buffer_2
  Shifter #(.width(32)) shifter_2 ();  // open: in, dist, out
  Register #(.width(32)) register_1 (.D(controlled_buffer_1_out), .en(or_2_out), .Q(lastOut), .clk(clk));  // open: clr
  assign xor_1_out = lastOut ^ xRow;  // XOR_Gate xor_1, 32 bits wide
  eq eq_2 (.A(lastOut), .B(32'hffc00000), .r(eq_2_r));
  assign full_2 = and_5_out ? eq_2_r : 1'bz;  // Controlled_Buffer controlled_buffer_3
  and and_5 (and_5_out, \union , cs);
  eq eq_3 (.A(lastOut), .B(and_6_out), .r(eq_3_r));
  assign and_6_out = lastOut & xor_1_out;  // AND_Gate and_6, 32 bits wide
  assign fail = and_7_out ? not_3_out : 1'bz;  // Controlled_Buffer controlled_buffer_4
  not not_3 (not_3_out, eq_3_r);
  and and_7 (and_7_out, check, cs);
  Adder #(.width(5)) adder_1 (.a(id), .b(5'b00001), .out(idNext));  // open: cin, cout

  assign checkOut = check;
  assign clkOut = clk;
  assign clrOut = clrMap;
  assign unionOut = \union ;
  assign xOut = xRow;
  assign yOut = y;

  // Other names for the same wires on the sheet: c = check; clr[31:0] = clrMap; current[31:0] = lastOut; u = \union ;
  //   X[31:0] = xRow
endmodule

module drawCell (
  input  [31:0] x,
  input  [4:0] y,
  input  [4:0] yIt,
  input  clk,
  input  cs,
  input  w,
  input  [7:0] nextFigure,
  output [31:0] _0,
  output [31:0] _0_2,
  output [31:0] _0_3,
  output [31:0] _0_4,
  output [31:0] _0_5,
  output [31:0] _0_6,
  output [31:0] _0_7,
  output [31:0] _0_8,
  output [31:0] _0_9,
  output [31:0] _0_10,
  output [31:0] _0_11,
  output [31:0] _0_12,
  output [31:0] _0_13,
  output [31:0] _0_14,
  output [31:0] _0_15,
  output [31:0] _0_16,
  output [31:0] _0_17,
  output [31:0] _0_18,
  output [31:0] _0_19,
  output [31:0] _0_20
);

  wire clk_t, r0, r1, r2, r3;
  wire [4:0] register_2_q, register_4_q, register_6_q, register_8_q, Y_t;
  wire [7:0] adder_2_out, counter_1_q, multiplier_1_out, rom_1_data, shift_register_1_q0, shift_register_1_q1;
  wire [31:0] _0_0, _0_1, _0_2_t, _0_3_t, _1_0, _1_1, _1_2, _1_3, _2_0, _2_1, _2_2, _2_3, _3_0, _3_1, _3_2,
       _3_3, _4_0, _4_1, _4_2, _4_3, _5_0, _5_1, _5_2, _5_3, _6_0, _6_1, _6_2, _6_3, _7_0, _7_1, _7_2, _7_3,
       _8_0, _8_1, _8_2, _8_3, _9_0, _9_1, _9_2, _9_3, _10_0, _10_1, _10_2, _10_3, _11_0, _11_1, _11_2,
       _11_3, _12_0, _12_1, _12_2, _12_3, _13_0, _13_1, _13_2, _13_3, _14_0, _14_1, _14_2, _14_3, _15_0,
       _15_1, _15_2, _15_3, _16_0, _16_1, _16_2, _16_3, _17_0, _17_1, _17_2, _17_3, _18_0, _18_1, _18_2,
       _18_3, _19_0, _19_1, _19_2, _19_3, fr0, fr1, fr2, fr3, register_1_q, register_3_q, register_5_q,
       register_7_q;

  Counter #(.width(1), .max('h1), .trigger("falling")) counter_1 (
    .Q(counter_1_q[0]), .clk(w));  // open: load, D, count, carry, clr
  assign clk_t = cs ? clk : 1'bz;  // Controlled_Buffer controlled_buffer_1
  Pull_Resistor pull_resistor_1 (.node(counter_1_q));
  Multiplier multiplier_1 (.a(8'h2), .b(nextFigure), .out(multiplier_1_out));  // open: cin, cout
  Shift_Register #(.width(8), .length(2)) shift_register_1 (
    .in(rom_1_data), .clk(w), .q0(shift_register_1_q0), .q1(shift_register_1_q1));  // open: shift, out, load, clr, d0, d1
  Adder #(.width(5)) adder_1 (.a(y), .b(yIt), .out(Y_t));  // open: cin, cout
  Adder adder_2 (.a(counter_1_q), .b(multiplier_1_out), .out(adder_2_out));  // open: cin, cout
  drawShifter drawshifter_1 (.in(shift_register_1_q1[7:4]), .out(fr0));
  drawShifter drawshifter_2 (.in(shift_register_1_q1[3:0]), .out(fr1));
  drawShifter drawshifter_3 (.in(shift_register_1_q0[7:4]), .out(fr2));
  drawShifter drawshifter_4 (.in(shift_register_1_q0[3:0]), .out(fr3));
  Decoder #(.select(2), .enable("false")) decoder_1 (.out0(r0), .out1(r1), .out2(r2), .out3(r3), .sel(yIt[1:0]));
  ROM rom_1 (.addr(adder_2_out), .data(rom_1_data));  // open: sel
  Register #(.width(32)) register_1 (.D(x), .en(r0), .Q(register_1_q), .clk(clk_t));  // open: clr
  Demultiplexer #(.select(5), .width(32), .enable("false")) demultiplexer_1 (
    .out0(_0_0), .out1(_1_0), .out2(_2_0), .out3(_3_0), .out4(_4_0), .out5(_5_0), .out6(_6_0), .out7(_7_0),
    .out8(_8_0), .out9(_9_0), .out10(_10_0), .out11(_11_0), .out12(_12_0), .out13(_13_0), .out14(_14_0),
    .out15(_15_0), .out16(_16_0), .out17(_17_0), .out18(_18_0), .out19(_19_0), .in(register_1_q),
    .sel(register_2_q));  // open: out20, out21, out22, out23, out24, out25, out26, out27, out28, out29, out30, out31
  Register #(.width(5)) register_2 (.D(Y_t), .en(r0), .Q(register_2_q), .clk(clk_t));  // open: clr
  Demultiplexer #(.select(5), .width(32), .enable("false")) demultiplexer_2 (
    .out0(_0_2_t), .out1(_1_2), .out2(_2_2), .out3(_3_2), .out4(_4_2), .out5(_5_2), .out6(_6_2), .out7(_7_2),
    .out8(_8_2), .out9(_9_2), .out10(_10_2), .out11(_11_2), .out12(_12_2), .out13(_13_2), .out14(_14_2),
    .out15(_15_2), .out16(_16_2), .out17(_17_2), .out18(_18_2), .out19(_19_2), .in(register_3_q),
    .sel(register_4_q));  // open: out20, out21, out22, out23, out24, out25, out26, out27, out28, out29, out30, out31
  Register #(.width(32)) register_3 (.D(x), .en(r2), .Q(register_3_q), .clk(clk_t));  // open: clr
  Register #(.width(5)) register_4 (.D(Y_t), .en(r2), .Q(register_4_q), .clk(clk_t));  // open: clr
  Demultiplexer #(.select(5), .width(32), .enable("false")) demultiplexer_3 (
    .out0(_0_1), .out1(_1_1), .out2(_2_1), .out3(_3_1), .out4(_4_1), .out5(_5_1), .out6(_6_1), .out7(_7_1),
    .out8(_8_1), .out9(_9_1), .out10(_10_1), .out11(_11_1), .out12(_12_1), .out13(_13_1), .out14(_14_1),
    .out15(_15_1), .out16(_16_1), .out17(_17_1), .out18(_18_1), .out19(_19_1), .in(register_5_q),
    .sel(register_6_q));  // open: out20, out21, out22, out23, out24, out25, out26, out27, out28, out29, out30, out31
  Register #(.width(32)) register_5 (.D(x), .en(r1), .Q(register_5_q), .clk(clk_t));  // open: clr
  Register #(.width(5)) register_6 (.D(Y_t), .en(r1), .Q(register_6_q), .clk(clk_t));  // open: clr
  Demultiplexer #(.select(5), .width(32), .enable("false")) demultiplexer_4 (
    .out0(_0_3_t), .out1(_1_3), .out2(_2_3), .out3(_3_3), .out4(_4_3), .out5(_5_3), .out6(_6_3), .out7(_7_3),
    .out8(_8_3), .out9(_9_3), .out10(_10_3), .out11(_11_3), .out12(_12_3), .out13(_13_3), .out14(_14_3),
    .out15(_15_3), .out16(_16_3), .out17(_17_3), .out18(_18_3), .out19(_19_3), .in(register_7_q),
    .sel(register_8_q));  // open: out20, out21, out22, out23, out24, out25, out26, out27, out28, out29, out30, out31
  Register #(.width(32)) register_7 (.D(x), .en(r3), .Q(register_7_q), .clk(clk_t));  // open: clr
  Register #(.width(5)) register_8 (.D(Y_t), .en(r3), .Q(register_8_q), .clk(clk_t));  // open: clr
  assign _0 = _0_0 | _0_1 | 32'h200000 | _0_2_t | _0_3_t;  // OR_Gate or_1, 32 bits wide
  assign _0_4 = _1_0 | _1_1 | 32'h200000 | _1_2 | _1_3;  // OR_Gate or_2, 32 bits wide
  assign _0_7 = _2_0 | _2_1 | 32'h200000 | _2_2 | _2_3;  // OR_Gate or_3, 32 bits wide
  assign _0_10 = _3_0 | _3_1 | 32'h200000 | _3_2 | _3_3;  // OR_Gate or_4, 32 bits wide
  assign _0_13 = _4_0 | _4_1 | 32'h200000 | _4_2 | _4_3;  // OR_Gate or_5, 32 bits wide
  assign _0_16 = _9_0 | _9_1 | 32'h200000 | _9_2 | _9_3;  // OR_Gate or_6, 32 bits wide
  assign _0_18 = _10_0 | _10_1 | 32'h200000 | _10_2 | _10_3;  // OR_Gate or_7, 32 bits wide
  assign _0_20 = _11_0 | _11_1 | 32'h200000 | _11_2 | _11_3;  // OR_Gate or_8, 32 bits wide
  assign _0_2 = _12_0 | _12_1 | 32'h200000 | _12_2 | _12_3;  // OR_Gate or_9, 32 bits wide
  assign _0_5 = _13_0 | _13_1 | 32'h200000 | _13_2 | _13_3;  // OR_Gate or_10, 32 bits wide
  assign _0_8 = _14_0 | _14_1 | 32'h200000 | _14_2 | _14_3;  // OR_Gate or_11, 32 bits wide
  assign _0_11 = _15_0 | _15_1 | 32'h200000 | _15_2 | _15_3;  // OR_Gate or_12, 32 bits wide
  assign _0_12 = _16_0 | _16_1 | 32'h200000 | _16_2 | _16_3;  // OR_Gate or_13, 32 bits wide
  assign _0_15 = _17_0 | _17_1 | 32'h200000 | _17_2 | _17_3;  // OR_Gate or_14, 32 bits wide
  assign _0_17 = _18_0 | _18_1 | 32'h200000 | _18_2 | _18_3;  // OR_Gate or_15, 32 bits wide
  assign _0_19 = _19_0 | _19_1 | 32'h200000 | _19_2 | _19_3;  // OR_Gate or_16, 32 bits wide
  assign _0_3 = 32'h200000 | _5_0 | _5_1 | _5_2 | _5_3 | fr0;  // OR_Gate or_17, 32 bits wide
  assign _0_6 = 32'h200000 | _6_0 | _6_1 | _6_2 | _6_3 | fr1;  // OR_Gate or_18, 32 bits wide
  assign _0_9 = 32'h200000 | _7_0 | _7_1 | _7_2 | _7_3 | fr2;  // OR_Gate or_19, 32 bits wide
  assign _0_14 = 32'h200000 | _8_0 | _8_1 | _8_2 | _8_3 | fr3;  // OR_Gate or_20, 32 bits wide

  // Other names for the same wires on the sheet: xRow[31:0] = x

  // Notes on the sheet:
  //   contents of rom_1 (hex, n*v repeats v):
  //   f 0 8e 0 2e 0 66 0 6c 0 4e 0 c6
endmodule

module ioreg (
  input  [7:0] in,
  input  addrEn,
  input  rw,
  input  clk,
  output [7:0] out,
  output [7:0] IOout
);

  wire and_1_out, and_2_out;

  assign IOout = and_1_out ? out : 8'bz;  // Controlled_Buffer controlled_buffer_1
  and and_1 (and_1_out, rw, addrEn);
  and and_2 (and_2_out, addrEn, ~rw);  // AND_Gate
  // Probe on out
  Register register_1 (.D(in), .en(and_2_out), .Q(out), .clk(clk));  // open: clr

  // Other names for the same wires on the sheet: X[7:0] = out
endmodule

module requestholder (
  input  [7:0] \input ,
  input  clk,
  input  req
);

  wire register_2_q;

  Register register_1 (.D(\input ), .clk(clk), .clr(register_2_q));  // open: en, Q
  Register #(.width(1), .trigger("falling")) register_2 (.D(req), .Q(register_2_q), .clk(clk));  // open: en, clr
endmodule

module scoreDisp (
  input  [31:0] bus_0,
  output [3:0] bus_0_2,
  output [31:0] bus_0_3
);

  wire [31:4] divider_1_rem;

  Divider #(.width(32)) divider_1 (.a(bus_0), .b(32'ha), .out(bus_0_3), .rem({divider_1_rem, bus_0_2}));  // open: upper
endmodule

module drawShifter (
  input  [3:0] in,
  output [31:0] out
);

  wire [27:0] pull_resistor_1_node;

  Pull_Resistor pull_resistor_1 (.node({in, pull_resistor_1_node}));
  Shifter #(.width(32), .shift("lr")) shifter_1 (.in({in, pull_resistor_1_node}), .\dist (5'b01100), .out(out));
endmodule

module ui (
);

  wire button_1_out, button_2_out, button_3_out, main_1_gameover;
  wire [3:0] main_1_bus_0_4, main_1_bus_0_5, main_1_bus_0_6, main_1_bus_0_7, main_1_bus_0_8, main_1_bus_0_9;

  Hex_Digit_Display hex_digit_display_1 (.value(main_1_bus_0_4));  // open: dp
  Hex_Digit_Display hex_digit_display_2 (.value(main_1_bus_0_5));  // open: dp
  Hex_Digit_Display hex_digit_display_3 (.value(main_1_bus_0_6));  // open: dp
  // _17x20_4_bit_LCD 17x20_4_bit_lcd_1: pin names not known
  Button button_1 (.out(button_1_out));
  Hex_Digit_Display hex_digit_display_4 (.value(main_1_bus_0_7));  // open: dp
  Button button_2 (.out(button_2_out));
  Hex_Digit_Display hex_digit_display_5 (.value(main_1_bus_0_8));  // open: dp
  Hex_Digit_Display hex_digit_display_6 (.value(main_1_bus_0_9));  // open: dp
  Button button_3 (.out(button_3_out));
  main main_1 (
    .bus_0_4(main_1_bus_0_4), .bus_0_5(main_1_bus_0_5), .bus_0_6(main_1_bus_0_6), .bus_0_7(main_1_bus_0_7),
    .bus_0_8(main_1_bus_0_8), .bus_0_9(main_1_bus_0_9), .bus_0(button_1_out), .bus_0_2(button_2_out),
    .bus_0_3(button_3_out), .gameOver(main_1_gameover));
  LED led_1 (.in(main_1_gameover));

  // Notes on the sheet:
  //   LEFT
  //   SCORE
  //   NEXT
  //   ROTATE
  //   RIGHT
  //   GAME OVER
endmodule
