// Logisim project scheme.circ as structural Verilog: 8 circuits, main circuit main
module main (
  input  [1:0] bus_0,
  input  [7:0] bus_0_2,
  input  bus_0_3,
  input  bus_0_4,
  input  bus_0_5,
  input  bus_0_6
);

  wire and_2_out, and_4_out, and_8_out, and_9_out, buffer_1_out, buffer_2_out, buffer_4_out, buffer_5_out,
       button_1_out, button_2_out, button_3_out, cdm_8_mark5_1_data_inst, cdm_8_mark5_1_mem_cycle,
       check_draw, clk, clr_new, comparator_1_eq, comparator_1_lt, comparator_2_eq, comparator_2_gt,
       comparator_2_lt, comparator_3_gt, coordsit_1_ready, csField, csFig, csVideo, decoder_1_out0,
       decoder_1_out1, IAck, IOflag, IOsel, IRQ, key, not_1_out, not_2_out, not_3_out, not_5_out, not_6_out,
       or_1_out, or_2_out, or_5_out, r, READwrite, screenClk, union_intersect, videoram_1_clr,
       videoram_1_csout, videoram_2_clr, videoram_2_csout, videoram_3_clr, videoram_3_csout, w;
  wire [1:0] rotDir;
  wire [2:0] figure_1_bus_0, figure_2_bus_0, vec;
  wire [7:0] addr, cdm_8_mark5_1_data_out, cdm_8_mark5_1_pc, cdm_8_mark5_1_ps, cdm_8_mark5_1_r0,
       cdm_8_mark5_1_r1, cdm_8_mark5_1_r2, cdm_8_mark5_1_r3, cdm_8_mark5_1_sp, controlled_buffer_2_out,
       coordsit_1_y, east_q, figure_1_fignext, figure_2_dataout, in, IOdat, out, pull_resistor_1_node,
       register_2_q, videoram_1_idout, videoram_1_rowo, videoram_2_idout, videoram_2_rowo, videoram_3_idout,
       videoram_3_rowo;
  wire [7:6] or_4_out;
  wire [31:0] coordsit_1_x, ui_1__1, ui_1__2, ui_1__3, ui_1__4, ui_1__5, ui_1__6, ui_1__7, ui_1__8, ui_1__9,
       ui_1__10, ui_1__11, ui_1__12, ui_1__13, ui_1__14, ui_1__15, ui_1__16, ui_1__17, ui_1__18, ui_1__19,
       ui_1__20, ui_1__21, ui_1__22, ui_1__23, ui_1__24, ui_1__25, ui_1__26, ui_1__27, ui_1__28, ui_1__29,
       ui_1__30, ui_1__31, ui_1__32, videoram_1_dataout, videoram_1_halted, videoram_1_halted_2,
       videoram_1_halted_3, videoram_1_halted_4, videoram_1_halted_5, videoram_1_halted_6,
       videoram_1_halted_7, videoram_1_halted_8, videoram_1_lastout, videoram_2_dataout, videoram_2_halted,
       videoram_2_halted_2, videoram_2_halted_3, videoram_2_halted_4, videoram_2_halted_5,
       videoram_2_halted_6, videoram_2_halted_7, videoram_2_halted_8, videoram_2_lastout, videoram_3_dataout,
       videoram_3_halted, videoram_3_halted_2, videoram_3_halted_3, videoram_3_halted_4, videoram_3_halted_5,
       videoram_3_halted_6, videoram_3_halted_7, videoram_3_halted_8, videoram_3_lastout, videoram_4_halted,
       videoram_4_halted_2, videoram_4_halted_3, videoram_4_halted_4, videoram_4_halted_5,
       videoram_4_halted_6, videoram_4_halted_7, videoram_4_halted_8;

  Comparator comparator_1 (.a(8'hf0), .b(addr), .eq(comparator_1_eq), .lt(comparator_1_lt));  // open: gt
  or or_1 (or_1_out, comparator_1_eq, comparator_1_lt);
  Comparator comparator_2 (.a(8'hf4), .b(addr), .gt(comparator_2_gt), .eq(comparator_2_eq), .lt(comparator_2_lt));
  or or_2 (or_2_out, comparator_2_eq, comparator_2_gt);
  and and_1 (IOflag, or_1_out, or_2_out);
  Clock clock_1 (.out(clk));
  and and_2 (and_2_out, IOsel, ~addr[0], ~addr[1], ~addr[2], ~addr[3]);  // AND_Gate
  Register register_1 (
    .D(IOdat), .en(and_2_out), .Q({rotDir, check_draw, clr_new, union_intersect, csVideo, csField, csFig}),
    .clk(clk));  // open: clr
  // Probe on cdm_8_mark5_1_r3
  // Probe on cdm_8_mark5_1_r2
  // Probe on cdm_8_mark5_1_r1
  // Probe on cdm_8_mark5_1_r0
  // Probe on cdm_8_mark5_1_sp
  // Probe on cdm_8_mark5_1_pc
  // Probe on cdm_8_mark5_1_ps
  CdM_8_mark5 cdm_8_mark5_1 (
    .clock(clk), .addr(addr), .mem_read(READwrite), .mem_cycle(cdm_8_mark5_1_mem_cycle),
    .data_inst(cdm_8_mark5_1_data_inst), .data_out(cdm_8_mark5_1_data_out),
    .data_in(controlled_buffer_2_out), .r0(cdm_8_mark5_1_r0), .r1(cdm_8_mark5_1_r1), .r2(cdm_8_mark5_1_r2),
    .r3(cdm_8_mark5_1_r3), .PC(cdm_8_mark5_1_pc), .SP(cdm_8_mark5_1_sp), .PS(cdm_8_mark5_1_ps), .IAck(IAck),
    .IRQ(IRQ), .vec(vec));  // open: stop
  and and_3 (IOsel, IOflag, decoder_1_out1);
  Decoder #(.disabled(0)) decoder_1 (
    .out0(decoder_1_out0), .out1(decoder_1_out1), .sel(cdm_8_mark5_1_data_inst), .en(cdm_8_mark5_1_mem_cycle));
  not not_1 (not_1_out, READwrite);
  assign IOdat = not_1_out ? cdm_8_mark5_1_data_out : 8'bz;  // Controlled_Buffer controlled_buffer_1
  assign controlled_buffer_2_out = READwrite ? IOdat : 8'bz;  // Controlled_Buffer controlled_buffer_2
  // Probe on addr
  and and_4 (and_4_out, decoder_1_out1, ~IOsel);  // AND_Gate
  and and_5 (w, IOsel, addr[0], ~addr[1], ~addr[2], ~addr[3]);  // AND_Gate
  assign IOdat = r ? out : 8'bz;  // Controlled_Buffer controlled_buffer_3
  and and_6 (r, IOsel, ~addr[0], addr[1], ~addr[2], ~addr[3]);  // AND_Gate
  assign in = w ? IOdat : 8'bz;  // Controlled_Buffer controlled_buffer_4
  RAM ram_1 (.addr(addr), .data(IOdat), .sel(and_4_out), .clk(not_2_out), .ld(READwrite));  // open: clr
  not not_2 (not_2_out, clk);
  ROM rom_1 (.addr(addr), .data(IOdat), .sel(decoder_1_out0));
  // Probe on IOdat
  and and_7 (key, IOsel, addr[0], addr[1], ~addr[2], ~addr[3]);  // AND_Gate
  // Probe on pull_resistor_1_node
  // NOR_Gate nor_1 is placed but not wired
  buf buffer_1 (buffer_1_out, buffer_2_out);
  buf buffer_2 (buffer_2_out, w);
  Pull_Resistor pull_resistor_1 (.node(pull_resistor_1_node));
  assign pull_resistor_1_node = in;  // Buffer buffer_3, 8 bits wide
  // Probe on register_2_q
  Register register_2 (.D(in), .en(csFig), .Q(register_2_q), .clk(buffer_4_out));  // open: clr
  buf buffer_4 (buffer_4_out, buffer_5_out);
  buf buffer_5 (buffer_5_out, buffer_1_out);
  figure figure_1 (
    .dir(rotDir), .r(r), .dataIn(pull_resistor_1_node), .dataOut(out), .figNext(figure_1_fignext),
    .cs(csFig), .\new (clr_new), .w(w), .bus_0(figure_1_bus_0));
  and and_8 (and_8_out, csVideo, w);
  LED led_1 (.in(csField));
  or or_3 (or_4_out[7], button_1_out, button_2_out);
  Button button_1 (.out(button_1_out));
  Button button_2 (.out(button_2_out));
  // Probe on out
  // Probe on in
  not not_3 (not_3_out, and_8_out);
  not not_4 (screenClk, not_3_out);
  field field_1 (
    .cs(csField), .clk(w), .\union (union_intersect), .clr(clr_new), .check(check_draw), .\input (in),
    .fail(out));
  or or_4 (or_4_out[6], button_2_out, button_3_out);
  Button button_3 (.out(button_3_out));
  // Probe on figure_1_fignext
  // Probe on figure_1_bus_0
  coordsIt coordsit_1 (.\input (in), .clk(screenClk), .X(coordsit_1_x), .Y(coordsit_1_y), .ready(coordsit_1_ready));
  // Probe on {or_4_out, {6{1'b0}}}
  not not_5 (not_5_out, not_6_out);
  not not_6 (not_6_out, key);
  Comparator comparator_3 (.a({or_4_out, {6{1'b0}}}), .b({8{1'b0}}), .gt(comparator_3_gt));  // open: eq, lt
  // Probe on figure_2_dataout
  figure figure_2 (
    .dir(bus_0), .r(bus_0_3), .dataIn(bus_0_2), .dataOut(figure_2_dataout), .cs(bus_0_4), .\new (bus_0_5),
    .w(bus_0_6), .bus_0(figure_2_bus_0));  // open: figNext
  or or_5 (or_5_out, clr_new, coordsit_1_ready);
  Register #(.trigger("falling")) east (
    .D({or_4_out, {6{1'b0}}}), .en(comparator_3_gt), .Q(east_q), .clk(not_5_out));  // open: clr
  assign out = key ? east_q : 8'bz;  // Controlled_Buffer controlled_buffer_5
  and and_9 (and_9_out, or_5_out, screenClk, union_intersect);
  // Probe on figure_2_bus_0
  videoRam videoram_1 (
    .csOUT(videoram_1_csout), .CS(and_9_out), .rowO(videoram_1_rowo), .halted(videoram_1_halted),
    .row(coordsit_1_y), .data(coordsit_1_x), .halted_2(videoram_1_halted_2), .clrRow(clr_new),
    .clr(videoram_1_clr), .halted_3(videoram_1_halted_3), .idIN({8{1'b0}}), .halted_4(videoram_1_halted_4),
    .dataOut(videoram_1_dataout), .halted_5(videoram_1_halted_5), .idOUT(videoram_1_idout),
    .halted_6(videoram_1_halted_6), .lastIn({32{1'b0}}), .halted_7(videoram_1_halted_7),
    .halted_8(videoram_1_halted_8), .lastOut(videoram_1_lastout));
  videoRam videoram_2 (
    .csOUT(videoram_2_csout), .CS(videoram_1_csout), .rowO(videoram_2_rowo), .halted(videoram_2_halted),
    .row(videoram_1_rowo), .data(videoram_1_dataout), .halted_2(videoram_2_halted_2),
    .clrRow(videoram_1_clr), .clr(videoram_2_clr), .halted_3(videoram_2_halted_3), .idIN(videoram_1_idout),
    .halted_4(videoram_2_halted_4), .dataOut(videoram_2_dataout), .halted_5(videoram_2_halted_5),
    .idOUT(videoram_2_idout), .halted_6(videoram_2_halted_6), .lastIn(videoram_1_lastout),
    .halted_7(videoram_2_halted_7), .halted_8(videoram_2_halted_8), .lastOut(videoram_2_lastout));
  videoRam videoram_3 (
    .csOUT(videoram_3_csout), .CS(videoram_2_csout), .rowO(videoram_3_rowo), .halted(videoram_3_halted),
    .row(videoram_2_rowo), .data(videoram_2_dataout), .halted_2(videoram_3_halted_2),
    .clrRow(videoram_2_clr), .clr(videoram_3_clr), .halted_3(videoram_3_halted_3), .idIN(videoram_2_idout),
    .halted_4(videoram_3_halted_4), .dataOut(videoram_3_dataout), .halted_5(videoram_3_halted_5),
    .idOUT(videoram_3_idout), .halted_6(videoram_3_halted_6), .lastIn(videoram_2_lastout),
    .halted_7(videoram_3_halted_7), .halted_8(videoram_3_halted_8), .lastOut(videoram_3_lastout));
  videoRam videoram_4 (
    .CS(videoram_3_csout), .halted(videoram_4_halted), .row(videoram_3_rowo), .data(videoram_3_dataout),
    .halted_2(videoram_4_halted_2), .clrRow(videoram_3_clr), .halted_3(videoram_4_halted_3),
    .idIN(videoram_3_idout), .halted_4(videoram_4_halted_4), .halted_5(videoram_4_halted_5),
    .halted_6(videoram_4_halted_6), .lastIn(videoram_3_lastout), .halted_7(videoram_4_halted_7),
    .halted_8(videoram_4_halted_8));  // open: csOUT, rowO, clr, dataOut, idOUT, lastOut
  // _32x32_4_bit_LCD 32x32_4_bit_lcd_1: pin names not known; wires that end beside it: union_intersect, videoram_1_halted, videoram_1_halted_2, videoram_1_halted_3, videoram_1_halted_4, videoram_1_halted_5, videoram_1_halted_6, videoram_1_halted_7, videoram_1_halted_8, videoram_2_halted, videoram_2_halted_2, videoram_2_halted_3, videoram_2_halted_4, videoram_2_halted_5, videoram_2_halted_6, videoram_2_halted_7, videoram_2_halted_8, videoram_3_halted, videoram_3_halted_2, videoram_3_halted_3, videoram_3_halted_4, videoram_3_halted_5, videoram_3_halted_6, videoram_3_halted_7, videoram_3_halted_8, videoram_4_halted, videoram_4_halted_2, videoram_4_halted_3, videoram_4_halted_4, videoram_4_halted_5, videoram_4_halted_6, videoram_4_halted_7, videoram_4_halted_8
  ui ui_1 (
    ._1(ui_1__1), ._17(ui_1__17), ._2(ui_1__2), ._18(ui_1__18), ._3(ui_1__3), ._19(ui_1__19), ._4(ui_1__4),
    ._20(ui_1__20), ._5(ui_1__5), ._21(ui_1__21), ._6(ui_1__6), ._22(ui_1__22), ._7(ui_1__7), ._23(ui_1__23),
    ._8(ui_1__8), ._24(ui_1__24), ._9(ui_1__9), ._25(ui_1__25), ._10(ui_1__10), ._26(ui_1__26),
    ._11(ui_1__11), ._27(ui_1__27), ._12(ui_1__12), ._28(ui_1__28), ._13(ui_1__13), ._29(ui_1__29),
    ._14(ui_1__14), ._30(ui_1__30), ._15(ui_1__15), ._31(ui_1__31), ._16(ui_1__16), ._32(ui_1__32),
    .cs(check_draw), .in(in), .clk(screenClk));

  // Other names for the same wires on the sheet: IOaddr[3:0] = addr[3:0]

  // Notes on the sheet:
  //   contents of rom_1 (hex, n*v repeats v):
  //   1 d0 f0 d1 11 a1 d1 1 a1 d6 35 d0 e8 d1 e0 d6 6a d6 af d0 0 f0 88 e0 31 c0 d0 f3 b1 5 e0 2e d0 c0 71
  //   e1 29 d6 76 ee 2e d0 1 54 d6 89 c4 ee 16 d6 76 ee 13 d0 f0 d1 11 a1 d0 f2 d2 e0 d1 9 89 e0 48 b3 ab
  //   8e ee 40 d0 f0 d1 0 a1 d7 d0 9 d1 e0 88 e0 69 b7 d2 f1 ab d2 f2 bb a7 c0 d0 ff 73 e1 65 ee 69 c4 8d
  //   ee 52 d7 d2 9 8a e0 75 b7 a3 8c 8d ee 6c d7 d0 f0 d1 c1 a1 d6 4e d1 ff 77 e1 86 d6 a8 d6 35 d6 af d7
  //   c0 d0 e8 d1 e0 d6 6a d0 f0 c5 a1 d6 4e d1 ff 77 e1 a5 d0 e0 d1 e8 d6 6a d6 a8 d6 35 d6 af d7 d1 e d2
  //   e8 d6 bb d7 d1 24 d2 e0 d6 bb d0 f0 d1 0 a1 d7 d0 f0 a1 9 d2 9 d0 f1 8a e0 cb b7 a3 8d ee c3 d7 d0
  //   f0 d1 22 a1 d0 e0 d1 f1 d2 5 8a e0 ec b3 a7 8c b3 a7 8c b7 c2 d2 1 4b e0 e9 ee ec c6 ee d7 d7 4*0 5
endmodule

module figure (
  input  [1:0] dir,
  input  cs,
  input  \new ,
  input  r,
  input  w,
  input  [7:0] dataIn,
  output [7:0] dataOut,
  output [7:0] figNext,
  output [2:0] bus_0
);

  wire and_1_out, and_2_out, and_4_out, and_5_out, and_6_out, and_7_out, and_8_out, and_9_out, and_10_out,
       and_11_out, and_12_out, and_13_out, and_14_out, and_15_out, and_16_out, buffer_1_out, buffer_2_out,
       buffer_3_out, buffer_4_out, comparator_1_eq, comparator_1_gt, comparator_2_eq, comparator_2_gt,
       comparator_3_eq, comparator_3_lt, dX, not_1_out, not_2_out, not_4_out, or_1_out, or_2_out, or_3_out,
       or_4_out, or_5_out, rotate;
  wire [1:0] counter_1_q;
  wire [7:0] adder_1_out, adder_6_out, adder_7_out, adder_8_out, controlled_buffer_7_out, out, rom_1_data,
       shifter;
  wire [8:0] adder_3_out, adder_4_out, adder_5_out, controlled_buffer_4_out, figNum, multiplier_1_out,
       multiplier_2_out, offset, random_1_out, rotOffset;
  wire [8:8] divider_1_rem;

  not not_1 (not_1_out, not_2_out);
  not not_2 (not_2_out, rotate);
  Register register_1 (.D(dataIn), .en(cs), .Q(shifter), .clk(buffer_1_out));  // open: clr
  buf buffer_1 (buffer_1_out, buffer_3_out);
  buf buffer_2 (buffer_2_out, buffer_4_out);
  buf buffer_3 (buffer_3_out, buffer_2_out);
  buf buffer_4 (buffer_4_out, w);
  and and_1 (and_1_out, dir[0], ~dir[1]);  // AND_Gate
  Counter #(.width(2), .max('h3), .trigger("falling")) counter_1 (
    .count(and_2_out), .Q(counter_1_q), .clk(or_1_out), .clr(\new ));  // open: load, D, carry
  and and_2 (and_2_out, cs, not_1_out);
  or or_1 (or_1_out, rotate, \new );
  and and_3 (rotate, ~dir[0], ~dir[1], cs, ~\new );  // AND_Gate
  and and_4 (and_4_out, dX, and_1_out);
  and and_5 (and_5_out, and_1_out, bus_0[0]);
  assign out = and_5_out ? shifter : 8'bz;  // Controlled_Buffer controlled_buffer_1
  Random #(.width(9)) random_1 (.clk(\new ), .out(random_1_out));  // open: next, clr
  assign out = and_4_out ? adder_1_out : 8'bz;  // Controlled_Buffer controlled_buffer_2
  Adder adder_1 (.a(8'h1), .b(shifter), .out(adder_1_out));  // open: cin, cout
  Multiplier #(.width(9)) multiplier_1 (.a(9'h20), .b(figNum), .out(multiplier_1_out));  // open: cin, cout
  Multiplier #(.width(9)) multiplier_2 (
    .a(9'h8), .b({{7{1'b0}}, counter_1_q}), .out(multiplier_2_out));  // open: cin, cout
  Divider #(.width(9)) divider_1 (.a(random_1_out), .b(9'h2), .rem({divider_1_rem[8], figNext}));  // open: out, upper
  // Probe on {divider_1_rem[8], figNext}
  Shift_Register shift_register_1 ();  // open: shift, in, clk, out, load, clr, d0, q0, d1, q1, d2, q2, d3, q3, d4, q4, d5, q5, d6, q6, d7, q7
  Multiplier #(.width(9)) multiplier_3 (.a(9'h8), .b(figNum), .out(offset));  // open: cin, cout
  Adder #(.width(9)) adder_2 (.a(multiplier_1_out), .b(multiplier_2_out), .out(rotOffset));  // open: cin, cout
  // Probe on figNum
  Register #(.width(9)) register_2 (.D({divider_1_rem[8], figNext}), .Q(figNum), .clk(and_6_out));  // open: en, clr
  and and_6 (and_6_out, cs, \new );
  Counter #(.width(3), .max('h7), .trigger("falling")) counter_2 (
    .load(1'b0), .D(3'b000), .count(cs), .Q(bus_0), .clk(r), .clr(1'b0));  // open: carry
  and and_7 (and_7_out, ~dir[0], dir[1]);  // AND_Gate
  not not_3 (dX, bus_0[0]);
  Adder #(.width(9)) adder_3 (.a({{6{1'b0}}, bus_0}), .b(9'h38), .out(adder_3_out));  // open: cin, cout
  Adder #(.width(9)) adder_4 (.a({{6{1'b0}}, bus_0}), .b(offset), .out(adder_4_out));  // open: cin, cout
  and and_8 (and_8_out, dX, and_7_out);
  and and_9 (and_9_out, and_7_out, bus_0[0]);
  assign out = and_9_out ? shifter : 8'bz;  // Controlled_Buffer controlled_buffer_3
  assign controlled_buffer_4_out = rotate ? adder_5_out : 9'bz;  // Controlled_Buffer controlled_buffer_4
  Adder #(.width(9)) adder_5 (.a(adder_3_out), .b(rotOffset), .out(adder_5_out));  // open: cin, cout
  assign controlled_buffer_4_out = \new  ? adder_4_out : 9'bz;  // Controlled_Buffer controlled_buffer_5
  Adder adder_6 (.a({8{1'b1}}), .b(shifter), .out(adder_6_out));  // open: cin, cout
  assign out = and_8_out ? adder_6_out : 8'bz;  // Controlled_Buffer controlled_buffer_6
  Comparator comparator_1 (.a(out), .b(8'h14), .gt(comparator_1_gt), .eq(comparator_1_eq));  // open: lt
  Comparator comparator_2 (.a(out), .b(8'ha), .gt(comparator_2_gt), .eq(comparator_2_eq));  // open: lt
  Comparator comparator_3 (.a(out), .b({8{1'b1}}), .eq(comparator_3_eq), .lt(comparator_3_lt));  // open: gt
  and and_10 (and_10_out, bus_0[0], or_2_out);
  or or_2 (or_2_out, comparator_1_gt, comparator_1_eq);
  and and_11 (and_11_out, dX, or_3_out);
  or or_3 (or_3_out, comparator_2_gt, comparator_2_eq);
  or or_4 (or_4_out, comparator_3_eq, comparator_3_lt);
  Adder adder_7 (.a(rom_1_data), .b(shifter), .out(adder_7_out));  // open: cin, cout
  assign controlled_buffer_7_out = or_5_out ? {8{1'b1}} : 8'bz;  // Controlled_Buffer controlled_buffer_7
  ROM #(.addrWidth(9)) rom_1 (.addr(controlled_buffer_4_out), .data(rom_1_data));  // open: sel
  and and_12 (and_12_out, bus_0[0], and_13_out);
  and and_13 (and_13_out, dir[0], dir[1]);
  and and_14 (and_14_out, and_13_out, dX);
  not not_4 (not_4_out, or_5_out);
  assign controlled_buffer_7_out = not_4_out ? out : 8'bz;  // Controlled_Buffer controlled_buffer_8
  or or_5 (or_5_out, and_10_out, and_11_out, or_4_out);
  assign out = \new  ? rom_1_data : 8'bz;  // Controlled_Buffer controlled_buffer_9
  assign out = rotate ? adder_7_out : 8'bz;  // Controlled_Buffer controlled_buffer_10
  Adder adder_8 (.a(8'h1), .b(shifter), .out(adder_8_out));  // open: cin, cout
  assign out = and_14_out ? shifter : 8'bz;  // Controlled_Buffer controlled_buffer_11
  assign dataOut = cs ? controlled_buffer_7_out : 8'bz;  // Controlled_Buffer controlled_buffer_12
  // Probe on out
  assign out = and_12_out ? adder_8_out : 8'bz;  // Controlled_Buffer controlled_buffer_13
  and and_15 (and_15_out, w, ~rotate, ~\new );  // AND_Gate
  // OR_Gate or_6 has open pins: in0=and_15_out, in1=and_16_out, out=open
  and and_16 (and_16_out, \new , r);

  // Other names for the same wires on the sheet: figNextNum[7:0] = figNext; dY = bus_0[0]; getNew = \new 

  // Notes on the sheet:
  //   MOVE RIGHT
  //   MOVE LEFT
  //   contents of rom_1 (hex, n*v repeats v):
  //   4 0 5 0 4 1 5 1 4 0 4 1 4 2 4 3 72*0 ff 1 0 0 1 ff 2 fe 2 ff 1 0 0 1 ff 2 fe 2 ff 1 0 0 1 ff 1 fe 0
  //   ff ff 0 fe 1
  //   MOVE DOWN
endmodule

module video (
  input  [7:0] coordsIn,
  input  cs,
  input  clk,
  input  draw,
  input  integrate,
  input  clrRow
);

  wire and_2_out, clk_t, coordsit_1_ready, or_1_out, videoram_1_clr, videoram_1_csout, videoram_2_clr,
       videoram_2_csout, videoram_3_clr, videoram_3_csout;
  wire [7:0] coordsit_1_y, videoram_1_idout, videoram_1_rowo, videoram_2_idout, videoram_2_rowo,
       videoram_3_idout, videoram_3_rowo;
  wire [31:0] coordsit_1_x, ui_1__1, ui_1__2, ui_1__3, ui_1__4, ui_1__5, ui_1__6, ui_1__7, ui_1__8, ui_1__9,
       ui_1__10, ui_1__11, ui_1__12, ui_1__13, ui_1__14, ui_1__15, ui_1__16, ui_1__17, ui_1__18, ui_1__19,
       ui_1__20, ui_1__21, ui_1__22, ui_1__23, ui_1__24, ui_1__25, ui_1__26, ui_1__27, ui_1__28, ui_1__29,
       ui_1__30, ui_1__31, ui_1__32, videoram_1_dataout, videoram_1_halted, videoram_1_halted_2,
       videoram_1_halted_3, videoram_1_halted_4, videoram_1_halted_5, videoram_1_halted_6,
       videoram_1_halted_7, videoram_1_halted_8, videoram_1_lastout, videoram_2_dataout, videoram_2_halted,
       videoram_2_halted_2, videoram_2_halted_3, videoram_2_halted_4, videoram_2_halted_5,
       videoram_2_halted_6, videoram_2_halted_7, videoram_2_halted_8, videoram_2_lastout, videoram_3_dataout,
       videoram_3_halted, videoram_3_halted_2, videoram_3_halted_3, videoram_3_halted_4, videoram_3_halted_5,
       videoram_3_halted_6, videoram_3_halted_7, videoram_3_halted_8, videoram_3_lastout, videoram_4_halted,
       videoram_4_halted_2, videoram_4_halted_3, videoram_4_halted_4, videoram_4_halted_5,
       videoram_4_halted_6, videoram_4_halted_7, videoram_4_halted_8;

  and and_1 (clk_t, cs, clk);
  coordsIt coordsit_1 (.\input (coordsIn), .clk(clk_t), .X(coordsit_1_x), .Y(coordsit_1_y), .ready(coordsit_1_ready));
  figure figure_1 ();  // open: dir, r, dataIn, dataOut, figNext, cs, new, w, bus_0
  or or_1 (or_1_out, clrRow, coordsit_1_ready);
  and and_2 (and_2_out, or_1_out, clk_t, integrate);
  videoRam videoram_1 (
    .csOUT(videoram_1_csout), .CS(and_2_out), .rowO(videoram_1_rowo), .halted(videoram_1_halted),
    .row(coordsit_1_y), .data(coordsit_1_x), .halted_2(videoram_1_halted_2), .clrRow(clrRow),
    .clr(videoram_1_clr), .halted_3(videoram_1_halted_3), .idIN({8{1'b0}}), .halted_4(videoram_1_halted_4),
    .dataOut(videoram_1_dataout), .halted_5(videoram_1_halted_5), .idOUT(videoram_1_idout),
    .halted_6(videoram_1_halted_6), .lastIn({32{1'b0}}), .halted_7(videoram_1_halted_7),
    .halted_8(videoram_1_halted_8), .lastOut(videoram_1_lastout));
  videoRam videoram_2 (
    .csOUT(videoram_2_csout), .CS(videoram_1_csout), .rowO(videoram_2_rowo), .halted(videoram_2_halted),
    .row(videoram_1_rowo), .data(videoram_1_dataout), .halted_2(videoram_2_halted_2),
    .clrRow(videoram_1_clr), .clr(videoram_2_clr), .halted_3(videoram_2_halted_3), .idIN(videoram_1_idout),
    .halted_4(videoram_2_halted_4), .dataOut(videoram_2_dataout), .halted_5(videoram_2_halted_5),
    .idOUT(videoram_2_idout), .halted_6(videoram_2_halted_6), .lastIn(videoram_1_lastout),
    .halted_7(videoram_2_halted_7), .halted_8(videoram_2_halted_8), .lastOut(videoram_2_lastout));
  videoRam videoram_3 (
    .csOUT(videoram_3_csout), .CS(videoram_2_csout), .rowO(videoram_3_rowo), .halted(videoram_3_halted),
    .row(videoram_2_rowo), .data(videoram_2_dataout), .halted_2(videoram_3_halted_2),
    .clrRow(videoram_2_clr), .clr(videoram_3_clr), .halted_3(videoram_3_halted_3), .idIN(videoram_2_idout),
    .halted_4(videoram_3_halted_4), .dataOut(videoram_3_dataout), .halted_5(videoram_3_halted_5),
    .idOUT(videoram_3_idout), .halted_6(videoram_3_halted_6), .lastIn(videoram_2_lastout),
    .halted_7(videoram_3_halted_7), .halted_8(videoram_3_halted_8), .lastOut(videoram_3_lastout));
  videoRam videoram_4 (
    .CS(videoram_3_csout), .halted(videoram_4_halted), .row(videoram_3_rowo), .data(videoram_3_dataout),
    .halted_2(videoram_4_halted_2), .clrRow(videoram_3_clr), .halted_3(videoram_4_halted_3),
    .idIN(videoram_3_idout), .halted_4(videoram_4_halted_4), .halted_5(videoram_4_halted_5),
    .halted_6(videoram_4_halted_6), .lastIn(videoram_3_lastout), .halted_7(videoram_4_halted_7),
    .halted_8(videoram_4_halted_8));  // open: csOUT, rowO, clr, dataOut, idOUT, lastOut
  // _32x32_4_bit_LCD 32x32_4_bit_lcd_1: pin names not known; wires that end beside it: videoram_1_halted, videoram_1_halted_2, videoram_1_halted_3, videoram_1_halted_4, videoram_1_halted_5, videoram_1_halted_6, videoram_1_halted_7, videoram_1_halted_8, videoram_2_halted, videoram_2_halted_2, videoram_2_halted_3, videoram_2_halted_4, videoram_2_halted_5, videoram_2_halted_6, videoram_2_halted_7, videoram_2_halted_8, videoram_3_halted, videoram_3_halted_2, videoram_3_halted_3, videoram_3_halted_4, videoram_3_halted_5, videoram_3_halted_6, videoram_3_halted_7, videoram_3_halted_8, videoram_4_halted, videoram_4_halted_2, videoram_4_halted_3, videoram_4_halted_4, videoram_4_halted_5, videoram_4_halted_6, videoram_4_halted_7, videoram_4_halted_8
  ui ui_1 (
    ._1(ui_1__1), ._17(ui_1__17), ._2(ui_1__2), ._18(ui_1__18), ._3(ui_1__3), ._19(ui_1__19), ._4(ui_1__4),
    ._20(ui_1__20), ._5(ui_1__5), ._21(ui_1__21), ._6(ui_1__6), ._22(ui_1__22), ._7(ui_1__7), ._23(ui_1__23),
    ._8(ui_1__8), ._24(ui_1__24), ._9(ui_1__9), ._25(ui_1__25), ._10(ui_1__10), ._26(ui_1__26),
    ._11(ui_1__11), ._27(ui_1__27), ._12(ui_1__12), ._28(ui_1__28), ._13(ui_1__13), ._29(ui_1__29),
    ._14(ui_1__14), ._30(ui_1__30), ._15(ui_1__15), ._31(ui_1__31), ._16(ui_1__16), ._32(ui_1__32),
    .cs(draw), .in(coordsIn), .clk(clk_t));

  // Other names for the same wires on the sheet: in[7:0] = coordsIn; integr = integrate
endmodule

module videoRam (
  input  CS,
  input  [7:0] row,
  input  [31:0] data,
  input  clrRow,
  input  [7:0] idIN,
  input  [31:0] lastIn,
  output csOUT,
  output [7:0] rowO,
  output [31:0] halted,
  output [31:0] halted_2,
  output clr,
  output [31:0] halted_3,
  output [31:0] halted_4,
  output [31:0] dataOut,
  output [31:0] halted_5,
  output [7:0] idOUT,
  output [31:0] halted_6,
  output [31:0] halted_7,
  output [31:0] halted_8,
  output [31:0] lastOut
);

  wire and_1_out, and_2_out, comparator_1_eq, comparator_1_lt, decoder_1_out0, decoder_1_out1,
       decoder_1_out2, decoder_1_out3, decoder_1_out4, decoder_1_out5, decoder_1_out6, decoder_1_out7,
       not_2_out, not_3_out, not_4_out, not_5_out, not_6_out, not_7_out, not_8_out, not_9_out, not_10_out,
       undriven;
  wire [2:0] adder_2_out;
  wire [7:0] controlled_buffer_1_out, divider_1_out, divider_1_rem, not_1_out, shifter_1_out;
  wire [31:0] controlled_buffer_11_out, controlled_buffer_12_out, controlled_buffer_13_out,
       controlled_buffer_14_out, controlled_buffer_15_out, controlled_buffer_16_out,
       controlled_buffer_17_out, controlled_buffer_18_out, or_1_out, or_2_out, or_3_out, or_4_out, or_5_out,
       or_6_out, or_7_out, or_8_out;

  Adder adder_1 (.a(8'h1), .b(idIN), .out(idOUT));  // open: cin, cout
  and and_1 (and_1_out, ~clrRow, comparator_1_eq);  // AND_Gate
  Divider divider_1 (.a(row), .b(8'h8), .out(divider_1_out), .rem(divider_1_rem));  // open: upper
  Decoder #(.select(3)) decoder_1 (
    .out0(decoder_1_out0), .out1(decoder_1_out1), .out2(decoder_1_out2), .out3(decoder_1_out3),
    .out4(decoder_1_out4), .out5(decoder_1_out5), .out6(decoder_1_out6), .out7(decoder_1_out7),
    .sel(divider_1_rem[2:0]), .en(and_1_out));
  Comparator comparator_1 (.a(idIN), .b(divider_1_out), .eq(comparator_1_eq), .lt(comparator_1_lt));  // open: gt
  // Probe on undriven
  Adder #(.width(3)) adder_2 (.a(divider_1_rem[2:0]), .b(3'b001), .out(adder_2_out));  // open: cin, cout
  assign not_1_out = ~shifter_1_out;  // NOT_Gate not_1, 8 bits wide
  not not_2 (not_2_out, and_2_out);
  assign controlled_buffer_1_out = not_2_out ? not_1_out : 8'bz;  // Controlled_Buffer controlled_buffer_1
  Shifter shifter_1 (.in({8{1'b1}}), .\dist (adder_2_out), .out(shifter_1_out));
  and and_2 (and_2_out, comparator_1_lt, clrRow);
  assign controlled_buffer_1_out = and_2_out ? {8{1'b1}} : 8'bz;  // Controlled_Buffer controlled_buffer_2
  Pull_Resistor pull_resistor_1 (.node(decoder_1_out0));
  Pull_Resistor pull_resistor_2 (.node(decoder_1_out1));
  Pull_Resistor pull_resistor_3 (.node(decoder_1_out2));
  Pull_Resistor pull_resistor_4 (.node(decoder_1_out3));
  Pull_Resistor pull_resistor_5 (.node(decoder_1_out4));
  Pull_Resistor pull_resistor_6 (.node(decoder_1_out5));
  Pull_Resistor pull_resistor_7 (.node(decoder_1_out6));
  Pull_Resistor pull_resistor_8 (.node(decoder_1_out7));
  assign decoder_1_out0 = clrRow ? controlled_buffer_1_out[0] : 1'bz;  // Controlled_Buffer controlled_buffer_3
  assign decoder_1_out1 = clrRow ? controlled_buffer_1_out[1] : 1'bz;  // Controlled_Buffer controlled_buffer_4
  assign decoder_1_out2 = clrRow ? controlled_buffer_1_out[2] : 1'bz;  // Controlled_Buffer controlled_buffer_5
  assign decoder_1_out3 = clrRow ? controlled_buffer_1_out[3] : 1'bz;  // Controlled_Buffer controlled_buffer_6
  assign decoder_1_out4 = clrRow ? controlled_buffer_1_out[4] : 1'bz;  // Controlled_Buffer controlled_buffer_7
  assign decoder_1_out5 = clrRow ? controlled_buffer_1_out[5] : 1'bz;  // Controlled_Buffer controlled_buffer_8
  assign decoder_1_out6 = clrRow ? controlled_buffer_1_out[6] : 1'bz;  // Controlled_Buffer controlled_buffer_9
  assign decoder_1_out7 = clrRow ? controlled_buffer_1_out[7] : 1'bz;  // Controlled_Buffer controlled_buffer_10
  not not_3 (not_3_out, clrRow);
  assign or_1_out = data | halted;  // OR_Gate or_1, 32 bits wide
  assign controlled_buffer_11_out = not_3_out ? or_1_out : 32'bz;  // Controlled_Buffer controlled_buffer_11
  not not_4 (not_4_out, clrRow);
  assign or_2_out = data | halted_2;  // OR_Gate or_2, 32 bits wide
  assign controlled_buffer_12_out = not_4_out ? or_2_out : 32'bz;  // Controlled_Buffer controlled_buffer_12
  not not_5 (not_5_out, clrRow);
  assign or_3_out = data | halted_3;  // OR_Gate or_3, 32 bits wide
  assign controlled_buffer_13_out = not_5_out ? or_3_out : 32'bz;  // Controlled_Buffer controlled_buffer_13
  not not_6 (not_6_out, clrRow);
  assign controlled_buffer_14_out = not_6_out ? or_4_out : 32'bz;  // Controlled_Buffer controlled_buffer_14
  assign or_4_out = data | halted_4;  // OR_Gate or_4, 32 bits wide
  not not_7 (not_7_out, clrRow);
  assign controlled_buffer_15_out = not_7_out ? or_5_out : 32'bz;  // Controlled_Buffer controlled_buffer_15
  assign or_5_out = data | halted_5;  // OR_Gate or_5, 32 bits wide
  not not_8 (not_8_out, clrRow);
  assign controlled_buffer_16_out = not_8_out ? or_6_out : 32'bz;  // Controlled_Buffer controlled_buffer_16
  assign or_6_out = data | halted_6;  // OR_Gate or_6, 32 bits wide
  not not_9 (not_9_out, clrRow);
  assign or_7_out = data | halted_7;  // OR_Gate or_7, 32 bits wide
  assign controlled_buffer_17_out = not_9_out ? or_7_out : 32'bz;  // Controlled_Buffer controlled_buffer_17
  not not_10 (not_10_out, clrRow);
  assign or_8_out = data | halted_8;  // OR_Gate or_8, 32 bits wide
  assign controlled_buffer_18_out = not_10_out ? or_8_out : 32'bz;  // Controlled_Buffer controlled_buffer_18
  assign controlled_buffer_11_out = clrRow ? lastIn : 32'bz;  // Controlled_Buffer controlled_buffer_19
  Register #(.width(32)) register_1 (
    .D(controlled_buffer_11_out), .en(decoder_1_out0), .Q(halted), .clk(CS));  // open: clr
  assign controlled_buffer_12_out = clrRow ? halted : 32'bz;  // Controlled_Buffer controlled_buffer_20
  Register #(.width(32)) register_2 (
    .D(controlled_buffer_12_out), .en(decoder_1_out1), .Q(halted_2), .clk(CS));  // open: clr
  assign controlled_buffer_13_out = clrRow ? halted_2 : 32'bz;  // Controlled_Buffer controlled_buffer_21
  Register #(.width(32)) register_3 (
    .D(controlled_buffer_13_out), .en(decoder_1_out2), .Q(halted_3), .clk(CS));  // open: clr
  assign controlled_buffer_14_out = clrRow ? halted_3 : 32'bz;  // Controlled_Buffer controlled_buffer_22
  Register #(.width(32)) register_4 (
    .D(controlled_buffer_14_out), .en(decoder_1_out3), .Q(halted_4), .clk(CS));  // open: clr
  assign controlled_buffer_15_out = clrRow ? halted_4 : 32'bz;  // Controlled_Buffer controlled_buffer_23
  Register #(.width(32)) register_5 (
    .D(controlled_buffer_15_out), .en(decoder_1_out4), .Q(halted_5), .clk(CS));  // open: clr
  assign controlled_buffer_16_out = clrRow ? halted_5 : 32'bz;  // Controlled_Buffer controlled_buffer_24
  Register #(.width(32)) register_6 (
    .D(controlled_buffer_16_out), .en(decoder_1_out5), .Q(halted_6), .clk(CS));  // open: clr
  assign controlled_buffer_17_out = clrRow ? halted_6 : 32'bz;  // Controlled_Buffer controlled_buffer_25
  Register #(.width(32)) register_7 (
    .D(controlled_buffer_17_out), .en(decoder_1_out6), .Q(halted_7), .clk(CS));  // open: clr
  assign controlled_buffer_18_out = clrRow ? halted_7 : 32'bz;  // Controlled_Buffer controlled_buffer_26
  Register #(.width(32)) register_8 (
    .D(controlled_buffer_18_out), .en(decoder_1_out7), .Q(halted_8), .clk(CS));  // open: clr

  assign clr = clrRow;
  assign csOUT = CS;
  assign dataOut = data;
  assign lastOut = halted_8;
  assign rowO = row;

  // Other names for the same wires on the sheet: id[7:0] = idIN
endmodule

module field (
  input  cs,
  input  clk,
  input  \union ,
  input  clr,
  input  check,
  input  [7:0] \input ,
  output [7:0] fail
);

  wire and_2_out, clk_t, fieldcell_1_check_2, fieldcell_1_clr_2, fieldcell_1_cs_2, fieldcell_1_union_2,
       fieldcell_2_check_2, fieldcell_2_clr_2, fieldcell_2_cs_2, fieldcell_2_union_2, fieldcell_3_check_2,
       fieldcell_3_clr_2, fieldcell_3_cs_2, fieldcell_3_union_2;
  wire [1:0] fieldcell_1_fail, fieldcell_2_fail, fieldcell_3_fail, fieldcell_4_fail, or_1_out;
  wire [2:0] counter_1_q;
  wire [7:0] fieldcell_1_id_2, fieldcell_1_row_2, fieldcell_2_id_2, fieldcell_2_row_2, fieldcell_3_id_2,
       fieldcell_3_row_2, register_1_q;
  wire [31:0] fieldcell_1_lastout, fieldcell_1_output, fieldcell_2_lastout, fieldcell_2_output,
       fieldcell_3_lastout, fieldcell_3_output, shifter_1_out;

  and and_1 (clk_t, cs, clk);
  Counter #(.width(3), .max('h0), .trigger("falling")) counter_1 (
    .Q(counter_1_q), .clk(clk_t));  // open: load, D, count, carry, clr
  Register register_1 (.D(\input ), .en(counter_1_q[0]), .Q(register_1_q), .clk(clk_t));  // open: clr
  and and_2 (and_2_out, clk_t, ~counter_1_q[0]);  // AND_Gate
  Shifter #(.width(32), .shift("lr")) shifter_1 (.in(32'h80000000), .\dist (register_1_q[4:0]), .out(shifter_1_out));
  fieldCell fieldcell_1 (
    .cs(and_2_out), .\union (\union ), .clr(clr), .check(check), .id({8{1'b0}}), .row(\input ),
    .\input (shifter_1_out), .lastIn({32{1'b0}}), .cs_2(fieldcell_1_cs_2), .union_2(fieldcell_1_union_2),
    .clr_2(fieldcell_1_clr_2), .check_2(fieldcell_1_check_2), .id_2(fieldcell_1_id_2),
    .row_2(fieldcell_1_row_2), .\output (fieldcell_1_output), .lastOut(fieldcell_1_lastout),
    .fail(fieldcell_1_fail));
  fieldCell fieldcell_2 (
    .cs(fieldcell_3_cs_2), .\union (fieldcell_3_union_2), .clr(fieldcell_3_clr_2),
    .check(fieldcell_3_check_2), .id(fieldcell_3_id_2), .row(fieldcell_3_row_2),
    .\input (fieldcell_3_output), .lastIn(fieldcell_3_lastout), .cs_2(fieldcell_2_cs_2),
    .union_2(fieldcell_2_union_2), .clr_2(fieldcell_2_clr_2), .check_2(fieldcell_2_check_2),
    .id_2(fieldcell_2_id_2), .row_2(fieldcell_2_row_2), .\output (fieldcell_2_output),
    .lastOut(fieldcell_2_lastout), .fail(fieldcell_2_fail));
  fieldCell fieldcell_3 (
    .cs(fieldcell_1_cs_2), .\union (fieldcell_1_union_2), .clr(fieldcell_1_clr_2),
    .check(fieldcell_1_check_2), .id(fieldcell_1_id_2), .row(fieldcell_1_row_2),
    .\input (fieldcell_1_output), .lastIn(fieldcell_1_lastout), .cs_2(fieldcell_3_cs_2),
    .union_2(fieldcell_3_union_2), .clr_2(fieldcell_3_clr_2), .check_2(fieldcell_3_check_2),
    .id_2(fieldcell_3_id_2), .row_2(fieldcell_3_row_2), .\output (fieldcell_3_output),
    .lastOut(fieldcell_3_lastout), .fail(fieldcell_3_fail));
  assign or_1_out = fieldcell_1_fail | fieldcell_3_fail | fieldcell_2_fail | fieldcell_4_fail;  // OR_Gate or_1, 2 bits wide
  assign fail = cs ? {{6{1'b0}}, or_1_out} : 8'bz;  // Controlled_Buffer controlled_buffer_1
  fieldCell fieldcell_4 (
    .cs(fieldcell_2_cs_2), .\union (fieldcell_2_union_2), .clr(fieldcell_2_clr_2),
    .check(fieldcell_2_check_2), .id(fieldcell_2_id_2), .row(fieldcell_2_row_2),
    .\input (fieldcell_2_output), .lastIn(fieldcell_2_lastout), .fail(fieldcell_4_fail));  // open: cs_2, union_2, clr_2, check_2, id_2, row_2, output, lastOut
endmodule

module fieldCell (
  input  cs,
  input  \union ,
  input  clr,
  input  check,
  input  [7:0] id,
  input  [7:0] row,
  input  [31:0] \input ,
  input  [31:0] lastIn,
  output cs_2,
  output union_2,
  output clr_2,
  output check_2,
  output [7:0] id_2,
  output [7:0] row_2,
  output [31:0] \output ,
  output [31:0] lastOut,
  output [1:0] fail
);

  wire and_1_out, and_2_out, and_3_out, and_4_out, and_5_out, and_6_out, and_7_out, and_8_out, and_9_out,
       and_10_out, and_11_out, comparator_1_eq, comparator_1_gt, comparator_2_eq, comparator_4_eq,
       comparator_6_eq, comparator_8_eq, comparator_10_eq, comparator_12_eq, comparator_14_eq,
       comparator_16_eq, or_1_out, or_2_out, or_3_out, or_4_out, or_5_out, or_6_out, or_7_out, or_8_out,
       or_9_out;
  wire [1:0] not_1_out, not_2_out, not_3_out, not_4_out, not_5_out, not_6_out, not_7_out, not_8_out;
  wire [2:0] adder_1_out;
  wire [7:0] decoder_1_out0, divider_1_out, divider_1_rem, shifter_1_out;
  wire [31:0] and_12_out, and_13_out, and_14_out, and_15_out, and_16_out, and_17_out, and_18_out, and_19_out,
       controlled_buffer_2_out, controlled_buffer_4_out, controlled_buffer_6_out, controlled_buffer_8_out,
       controlled_buffer_10_out, controlled_buffer_12_out, controlled_buffer_14_out,
       controlled_buffer_16_out, or_10_out, or_11_out, or_12_out, or_13_out, or_14_out, or_15_out, or_16_out,
       or_17_out, register_1_q, register_2_q, register_3_q, register_4_q, register_5_q, register_6_q,
       register_7_q, xor_1_out, xor_2_out, xor_3_out, xor_4_out, xor_5_out, xor_6_out, xor_7_out, xor_8_out;

  Divider divider_1 (.a(row), .b(8'h8), .out(divider_1_out), .rem(divider_1_rem));  // open: upper
  Comparator comparator_1 (.a(divider_1_out), .b(id), .gt(comparator_1_gt), .eq(comparator_1_eq));  // open: lt
  and and_1 (and_1_out, comparator_1_eq, or_1_out);
  or or_1 (or_1_out, \union , check);
  Adder #(.width(3)) adder_1 (.a(divider_1_rem[2:0]), .b(3'b001), .out(adder_1_out));  // open: cin, cout
  Decoder #(.select(3)) decoder_1 (
    .out0(decoder_1_out0[0]), .out1(decoder_1_out0[1]), .out2(decoder_1_out0[2]), .out3(decoder_1_out0[3]),
    .out4(decoder_1_out0[4]), .out5(decoder_1_out0[5]), .out6(decoder_1_out0[6]), .out7(decoder_1_out0[7]),
    .sel(divider_1_rem[2:0]), .en(and_1_out));
  and and_2 (and_2_out, clr, comparator_1_eq);
  Shifter shifter_1 (.in({8{1'b1}}), .\dist (adder_1_out), .out(shifter_1_out));
  assign decoder_1_out0 = and_2_out ? ~shifter_1_out : 8'bz;  // Controlled_Inverter controlled_inverter_1
  assign decoder_1_out0 = and_3_out ? {8{1'b1}} : 8'bz;  // Controlled_Buffer controlled_buffer_1
  and and_3 (and_3_out, comparator_1_gt, clr);
  Pull_Resistor pull_resistor_1 (.node(decoder_1_out0[0]));
  Pull_Resistor pull_resistor_2 (.node(decoder_1_out0[1]));
  Pull_Resistor pull_resistor_3 (.node(decoder_1_out0[2]));
  Pull_Resistor pull_resistor_4 (.node(decoder_1_out0[3]));
  Pull_Resistor pull_resistor_5 (.node(decoder_1_out0[4]));
  Pull_Resistor pull_resistor_6 (.node(decoder_1_out0[5]));
  Pull_Resistor pull_resistor_7 (.node(decoder_1_out0[6]));
  Pull_Resistor pull_resistor_8 (.node(decoder_1_out0[7]));
  or or_2 (or_2_out, \union , clr);
  and and_4 (and_4_out, or_2_out, decoder_1_out0[0]);
  or or_3 (or_3_out, \union , clr);
  and and_5 (and_5_out, or_3_out, decoder_1_out0[1]);
  or or_4 (or_4_out, \union , clr);
  and and_6 (and_6_out, or_4_out, decoder_1_out0[2]);
  or or_5 (or_5_out, \union , clr);
  and and_7 (and_7_out, or_5_out, decoder_1_out0[3]);
  or or_6 (or_6_out, \union , clr);
  and and_8 (and_8_out, or_6_out, decoder_1_out0[4]);
  or or_7 (or_7_out, \union , clr);
  and and_9 (and_9_out, or_7_out, decoder_1_out0[5]);
  or or_8 (or_8_out, \union , clr);
  and and_10 (and_10_out, or_8_out, decoder_1_out0[6]);
  or or_9 (or_9_out, \union , clr);
  and and_11 (and_11_out, or_9_out, decoder_1_out0[7]);
  assign controlled_buffer_2_out = clr ? lastIn : 32'bz;  // Controlled_Buffer controlled_buffer_2
  assign controlled_buffer_2_out = \union  ? or_10_out : 32'bz;  // Controlled_Buffer controlled_buffer_3
  assign or_10_out = \input  | register_1_q;  // OR_Gate or_10, 32 bits wide
  assign controlled_buffer_4_out = clr ? register_1_q : 32'bz;  // Controlled_Buffer controlled_buffer_4
  assign or_11_out = \input  | register_2_q;  // OR_Gate or_11, 32 bits wide
  assign controlled_buffer_4_out = \union  ? or_11_out : 32'bz;  // Controlled_Buffer controlled_buffer_5
  assign controlled_buffer_6_out = clr ? register_2_q : 32'bz;  // Controlled_Buffer controlled_buffer_6
  assign or_12_out = \input  | register_3_q;  // OR_Gate or_12, 32 bits wide
  assign controlled_buffer_6_out = \union  ? or_12_out : 32'bz;  // Controlled_Buffer controlled_buffer_7
  assign controlled_buffer_8_out = clr ? register_3_q : 32'bz;  // Controlled_Buffer controlled_buffer_8
  assign controlled_buffer_8_out = \union  ? or_13_out : 32'bz;  // Controlled_Buffer controlled_buffer_9
  assign or_13_out = \input  | register_4_q;  // OR_Gate or_13, 32 bits wide
  assign controlled_buffer_10_out = clr ? register_4_q : 32'bz;  // Controlled_Buffer controlled_buffer_10
  assign controlled_buffer_10_out = \union  ? or_14_out : 32'bz;  // Controlled_Buffer controlled_buffer_11
  assign or_14_out = \input  | register_5_q;  // OR_Gate or_14, 32 bits wide
  assign controlled_buffer_12_out = clr ? register_5_q : 32'bz;  // Controlled_Buffer controlled_buffer_12
  assign or_15_out = \input  | register_6_q;  // OR_Gate or_15, 32 bits wide
  assign controlled_buffer_12_out = \union  ? or_15_out : 32'bz;  // Controlled_Buffer controlled_buffer_13
  assign controlled_buffer_14_out = clr ? register_6_q : 32'bz;  // Controlled_Buffer controlled_buffer_14
  assign controlled_buffer_14_out = \union  ? or_16_out : 32'bz;  // Controlled_Buffer controlled_buffer_15
  assign or_16_out = \input  | register_7_q;  // OR_Gate or_16, 32 bits wide
  assign controlled_buffer_16_out = clr ? register_7_q : 32'bz;  // Controlled_Buffer controlled_buffer_16
  assign or_17_out = \input  | lastOut;  // OR_Gate or_17, 32 bits wide
  assign controlled_buffer_16_out = \union  ? or_17_out : 32'bz;  // Controlled_Buffer controlled_buffer_17
  Register #(.width(32)) register_1 (
    .D(controlled_buffer_2_out), .en(and_4_out), .Q(register_1_q), .clk(cs));  // open: clr
  Register #(.width(32)) register_2 (
    .D(controlled_buffer_4_out), .en(and_5_out), .Q(register_2_q), .clk(cs));  // open: clr
  Register #(.width(32)) register_3 (
    .D(controlled_buffer_6_out), .en(and_6_out), .Q(register_3_q), .clk(cs));  // open: clr
  Register #(.width(32)) register_4 (
    .D(controlled_buffer_8_out), .en(and_7_out), .Q(register_4_q), .clk(cs));  // open: clr
  Register #(.width(32)) register_5 (
    .D(controlled_buffer_10_out), .en(and_8_out), .Q(register_5_q), .clk(cs));  // open: clr
  Register #(.width(32)) register_6 (
    .D(controlled_buffer_12_out), .en(and_9_out), .Q(register_6_q), .clk(cs));  // open: clr
  Register #(.width(32)) register_7 (
    .D(controlled_buffer_14_out), .en(and_10_out), .Q(register_7_q), .clk(cs));  // open: clr
  Register #(.width(32)) register_8 (
    .D(controlled_buffer_16_out), .en(and_11_out), .Q(lastOut), .clk(cs));  // open: clr
  assign xor_1_out = \input  ^ register_1_q;  // XOR_Gate xor_1, 32 bits wide
  assign and_12_out = xor_1_out & register_1_q;  // AND_Gate and_12, 32 bits wide
  assign xor_2_out = \input  ^ register_2_q;  // XOR_Gate xor_2, 32 bits wide
  assign and_13_out = xor_2_out & register_2_q;  // AND_Gate and_13, 32 bits wide
  assign xor_3_out = \input  ^ register_3_q;  // XOR_Gate xor_3, 32 bits wide
  assign and_14_out = xor_3_out & register_3_q;  // AND_Gate and_14, 32 bits wide
  assign xor_4_out = \input  ^ register_4_q;  // XOR_Gate xor_4, 32 bits wide
  assign and_15_out = xor_4_out & register_4_q;  // AND_Gate and_15, 32 bits wide
  assign xor_5_out = \input  ^ register_5_q;  // XOR_Gate xor_5, 32 bits wide
  assign and_16_out = xor_5_out & register_5_q;  // AND_Gate and_16, 32 bits wide
  assign xor_6_out = \input  ^ register_6_q;  // XOR_Gate xor_6, 32 bits wide
  assign and_17_out = xor_6_out & register_6_q;  // AND_Gate and_17, 32 bits wide
  assign xor_7_out = \input  ^ register_7_q;  // XOR_Gate xor_7, 32 bits wide
  assign and_18_out = xor_7_out & register_7_q;  // AND_Gate and_18, 32 bits wide
  assign xor_8_out = \input  ^ lastOut;  // XOR_Gate xor_8, 32 bits wide
  assign and_19_out = xor_8_out & lastOut;  // AND_Gate and_19, 32 bits wide
  Comparator #(.width(32)) comparator_2 (.a(and_12_out), .b(register_1_q), .eq(comparator_2_eq));  // open: gt, lt
  not not_1 (not_1_out[0], comparator_2_eq);
  Comparator #(.width(32)) comparator_3 (.a(register_1_q), .b(32'hffc00000), .eq(not_1_out[1]));  // open: gt, lt
  Comparator #(.width(32)) comparator_4 (.a(and_13_out), .b(register_2_q), .eq(comparator_4_eq));  // open: gt, lt
  not not_2 (not_2_out[0], comparator_4_eq);
  Comparator #(.width(32)) comparator_5 (.a(register_2_q), .b(32'hffc00000), .eq(not_2_out[1]));  // open: gt, lt
  Comparator #(.width(32)) comparator_6 (.a(and_14_out), .b(register_3_q), .eq(comparator_6_eq));  // open: gt, lt
  not not_3 (not_3_out[0], comparator_6_eq);
  Comparator #(.width(32)) comparator_7 (.a(register_3_q), .b(32'hffc00000), .eq(not_3_out[1]));  // open: gt, lt
  Comparator #(.width(32)) comparator_8 (.a(and_15_out), .b(register_4_q), .eq(comparator_8_eq));  // open: gt, lt
  not not_4 (not_4_out[0], comparator_8_eq);
  Comparator #(.width(32)) comparator_9 (.a(register_4_q), .b(32'hffc00000), .eq(not_4_out[1]));  // open: gt, lt
  Comparator #(.width(32)) comparator_10 (.a(and_16_out), .b(register_5_q), .eq(comparator_10_eq));  // open: gt, lt
  not not_5 (not_5_out[0], comparator_10_eq);
  Comparator #(.width(32)) comparator_11 (.a(register_5_q), .b(32'hffc00000), .eq(not_5_out[1]));  // open: gt, lt
  Comparator #(.width(32)) comparator_12 (.a(and_17_out), .b(register_6_q), .eq(comparator_12_eq));  // open: gt, lt
  not not_6 (not_6_out[0], comparator_12_eq);
  Comparator #(.width(32)) comparator_13 (.a(register_6_q), .b(32'hffc00000), .eq(not_6_out[1]));  // open: gt, lt
  Comparator #(.width(32)) comparator_14 (.a(and_18_out), .b(register_7_q), .eq(comparator_14_eq));  // open: gt, lt
  not not_7 (not_7_out[0], comparator_14_eq);
  Comparator #(.width(32)) comparator_15 (.a(register_7_q), .b(32'hffc00000), .eq(not_7_out[1]));  // open: gt, lt
  Comparator #(.width(32)) comparator_16 (.a(and_19_out), .b(lastOut), .eq(comparator_16_eq));  // open: gt, lt
  not not_8 (not_8_out[0], comparator_16_eq);
  Comparator #(.width(32)) comparator_17 (.a(lastOut), .b(32'hffc00000), .eq(not_8_out[1]));  // open: gt, lt
  assign fail = decoder_1_out0[0] ? not_1_out : 2'bz;  // Controlled_Buffer controlled_buffer_18
  assign fail = decoder_1_out0[1] ? not_2_out : 2'bz;  // Controlled_Buffer controlled_buffer_19
  assign fail = decoder_1_out0[2] ? not_3_out : 2'bz;  // Controlled_Buffer controlled_buffer_20
  assign fail = decoder_1_out0[3] ? not_4_out : 2'bz;  // Controlled_Buffer controlled_buffer_21
  assign fail = decoder_1_out0[4] ? not_5_out : 2'bz;  // Controlled_Buffer controlled_buffer_22
  assign fail = decoder_1_out0[5] ? not_6_out : 2'bz;  // Controlled_Buffer controlled_buffer_23
  assign fail = decoder_1_out0[6] ? not_7_out : 2'bz;  // Controlled_Buffer controlled_buffer_24
  assign fail = decoder_1_out0[7] ? not_8_out : 2'bz;  // Controlled_Buffer controlled_buffer_25
  Pull_Resistor pull_resistor_9 (.node(fail));
  Adder adder_2 (.a(id), .b(8'h1), .out(id_2));  // open: cin, cout

  assign check_2 = check;
  assign clr_2 = clr;
  assign cs_2 = cs;
  assign \output  = \input ;
  assign row_2 = row;
  assign union_2 = \union ;

  // Other names for the same wires on the sheet: data[31:0] = \input 
endmodule

module coordsIt (
  input  [7:0] \input ,
  input  clk,
  output [31:0] X,
  output [7:0] Y,
  output ready
);

  wire not_1_out;
  wire [2:1] counter_1_q;
  wire [7:0] register_1_q;

  Counter #(.width(3), .max('h7), .trigger("falling")) counter_1 (
    .Q({counter_1_q, ready}), .clk(clk));  // open: load, D, count, carry, clr
  not not_1 (not_1_out, ready);
  Register register_1 (.D(\input ), .en(not_1_out), .Q(register_1_q), .clk(clk));  // open: clr
  Shifter #(.width(32), .shift("lr")) shifter_1 (.in(32'h80000000), .\dist (register_1_q[4:0]), .out(X));

  assign Y = \input ;
endmodule

module ui (
  input  cs,
  input  clk,
  input  [7:0] in,
  output [31:0] _1,
  output [31:0] _17,
  output [31:0] _2,
  output [31:0] _18,
  output [31:0] _3,
  output [31:0] _19,
  output [31:0] _4,
  output [31:0] _20,
  output [31:0] _5,
  output [31:0] _21,
  output [31:0] _6,
  output [31:0] _22,
  output [31:0] _7,
  output [31:0] _23,
  output [31:0] _8,
  output [31:0] _24,
  output [31:0] _9,
  output [31:0] _25,
  output [31:0] _10,
  output [31:0] _26,
  output [31:0] _11,
  output [31:0] _27,
  output [31:0] _12,
  output [31:0] _28,
  output [31:0] _13,
  output [31:0] _29,
  output [31:0] _14,
  output [31:0] _30,
  output [31:0] _15,
  output [31:0] _31,
  output [31:0] _16,
  output [31:0] _32
);

  wire controlled_buffer_1_out, ncs;
  wire [4:0] _1X, _1Y, _2X, _2Y, _3X, _3Y, _4X, _4Y, buffer_1_out, buffer_2_out, buffer_3_out, buffer_4_out,
       buffer_5_out, buffer_6_out, buffer_7_out, buffer_8_out, buffer_9_out, buffer_10_out, buffer_11_out,
       buffer_12_out, buffer_13_out, buffer_14_out, buffer_15_out, buffer_16_out, buffer_17_out,
       buffer_18_out, buffer_19_out, buffer_20_out, buffer_21_out, buffer_22_out, buffer_23_out,
       buffer_24_out, buffer_25_out, buffer_26_out, buffer_27_out, buffer_28_out, buffer_29_out,
       buffer_30_out, buffer_31_out, buffer_32_out, register_1_q, register_2_q, register_3_q, register_4_q,
       register_5_q, register_6_q, register_7_q, register_8_q, shift_register_1_out;
  wire [31:0] _0_01, _0_02, _0_03, _0_04, _0_05, _0_06, _0_07, _0_08, _0_09, _0_10, _0_11, _0_12, _0_13,
       _0_14, _0_15, _0_16, _0_17, _0_18, _0_19, _0_20, _0_21, _0_22, _0_23, _0_24, _0_25, _0_26, _0_27,
       _0_28, _0_29, _0_30, _0_31, _0_32, _1_01, _1_02, _1_03, _1_04, _1_05, _1_06, _1_07, _1_08, _1_09,
       _1_10, _1_11, _1_12, _1_13, _1_14, _1_15, _1_16, _1_17, _1_18, _1_19, _1_20, _1_21, _1_22, _1_23,
       _1_24, _1_25, _1_26, _1_27, _1_28, _1_29, _1_30, _1_31, _1_32, _2_01, _2_02, _2_03, _2_04, _2_05,
       _2_06, _2_07, _2_08, _2_09, _2_10, _2_11, _2_12, _2_13, _2_14, _2_15, _2_16, _2_17, _2_18, _2_19,
       _2_20, _2_21, _2_22, _2_23, _2_24, _2_25, _2_26, _2_27, _2_28, _2_29, _2_30, _2_31, _2_32, _3_01,
       _3_02, _3_03, _3_04, _3_05, _3_06, _3_07, _3_08, _3_09, _3_10, _3_11, _3_12, _3_13, _3_14, _3_15,
       _3_16, _3_17, _3_18, _3_19, _3_20, _3_21, _3_22, _3_23, _3_24, _3_25, _3_26, _3_27, _3_28, _3_29,
       _3_30, _3_31, _3_32, shifter_1_out, shifter_2_out, shifter_3_out, shifter_4_out;

  assign _1 = _0_01 | _1_01 | _2_01 | _3_01;  // OR_Gate or_1, 32 bits wide
  assign _2 = _0_02 | _1_02 | _2_02 | _3_02;  // OR_Gate or_2, 32 bits wide
  assign _3 = _0_03 | _1_03 | _2_03 | _3_03;  // OR_Gate or_3, 32 bits wide
  assign _4 = _0_04 | _1_04 | _2_04 | _3_04;  // OR_Gate or_4, 32 bits wide
  assign _5 = _0_05 | _1_05 | _2_05 | _3_05;  // OR_Gate or_5, 32 bits wide
  assign _6 = _0_06 | _1_06 | _2_06 | _3_06;  // OR_Gate or_6, 32 bits wide
  assign _7 = _0_07 | _1_07 | _2_07 | _3_07;  // OR_Gate or_7, 32 bits wide
  assign _8 = _0_08 | _1_08 | _2_08 | _3_08;  // OR_Gate or_8, 32 bits wide
  assign _9 = _0_09 | _1_09 | _2_09 | _3_09;  // OR_Gate or_9, 32 bits wide
  assign _10 = _0_10 | _1_10 | _2_10 | _3_10;  // OR_Gate or_10, 32 bits wide
  assign _11 = _0_11 | _1_11 | _2_11 | _3_11;  // OR_Gate or_11, 32 bits wide
  assign _12 = _0_12 | _1_12 | _2_12 | _3_12;  // OR_Gate or_12, 32 bits wide
  assign _13 = _0_13 | _1_13 | _2_13 | _3_13;  // OR_Gate or_13, 32 bits wide
  assign _14 = _0_14 | _1_14 | _2_14 | _3_14;  // OR_Gate or_14, 32 bits wide
  assign _15 = _0_15 | _1_15 | _2_15 | _3_15;  // OR_Gate or_15, 32 bits wide
  assign _16 = _0_16 | _1_16 | _2_16 | _3_16;  // OR_Gate or_16, 32 bits wide
  assign _17 = _0_17 | _1_17 | _2_17 | _3_17;  // OR_Gate or_17, 32 bits wide
  assign _18 = _0_18 | _1_18 | _2_18 | _3_18;  // OR_Gate or_18, 32 bits wide
  assign _19 = _0_19 | _1_19 | _2_19 | _3_19;  // OR_Gate or_19, 32 bits wide
  assign _20 = _0_20 | _1_20 | _2_20 | _3_20;  // OR_Gate or_20, 32 bits wide
  assign _21 = _0_21 | _1_21 | _2_21 | _3_21;  // OR_Gate or_21, 32 bits wide
  assign _22 = _0_22 | _1_22 | _2_22 | _3_22;  // OR_Gate or_22, 32 bits wide
  assign _23 = _0_23 | _1_23 | _2_23 | _3_23;  // OR_Gate or_23, 32 bits wide
  assign _24 = _0_24 | _1_24 | _2_24 | _3_24;  // OR_Gate or_24, 32 bits wide
  assign _25 = _0_25 | _1_25 | _2_25 | _3_25;  // OR_Gate or_25, 32 bits wide
  assign _26 = _0_26 | _1_26 | _2_26 | _3_26;  // OR_Gate or_26, 32 bits wide
  assign _27 = _0_27 | _1_27 | _2_27 | _3_27;  // OR_Gate or_27, 32 bits wide
  assign _28 = _0_28 | _1_28 | _2_28 | _3_28;  // OR_Gate or_28, 32 bits wide
  assign _29 = _0_29 | _1_29 | _2_29 | _3_29;  // OR_Gate or_29, 32 bits wide
  assign _30 = _0_30 | _1_30 | _2_30 | _3_30;  // OR_Gate or_30, 32 bits wide
  assign _31 = _0_31 | _1_31 | _2_31 | _3_31;  // OR_Gate or_31, 32 bits wide
  assign _32 = _0_32 | _1_32 | _2_32 | _3_32;  // OR_Gate or_32, 32 bits wide
  assign controlled_buffer_1_out = cs ? clk : 1'bz;  // Controlled_Buffer controlled_buffer_1
  Shift_Register #(.width(5)) shift_register_1 (
    .shift(1'b1), .in(in[4:0]), .clk(controlled_buffer_1_out), .out(shift_register_1_out), .q0(_4Y),
    .q1(_4X), .q2(_3Y), .q3(_3X), .q4(_2Y), .q5(_2X), .q6(_1Y), .q7(_1X));  // open: load, clr, d0, d1, d2, d3, d4, d5, d6, d7
  Pull_Resistor pull_resistor_1 (.node(controlled_buffer_1_out));
  not not_1 (ncs, cs);
  assign buffer_1_out = _2X;  // Buffer buffer_1, 5 bits wide
  assign buffer_2_out = buffer_1_out;  // Buffer buffer_2, 5 bits wide
  assign buffer_3_out = buffer_4_out;  // Buffer buffer_3, 5 bits wide
  assign buffer_4_out = _3X;  // Buffer buffer_4, 5 bits wide
  Register #(.width(5), .trigger("falling")) register_1 (
    .D(buffer_5_out), .Q(register_1_q), .clk(ncs));  // open: en, clr
  assign buffer_5_out = buffer_6_out;  // Buffer buffer_5, 5 bits wide
  assign buffer_6_out = buffer_2_out;  // Buffer buffer_6, 5 bits wide
  assign buffer_7_out = _2Y;  // Buffer buffer_7, 5 bits wide
  assign buffer_8_out = buffer_9_out;  // Buffer buffer_8, 5 bits wide
  Register #(.width(5), .trigger("falling")) register_2 (
    .D(buffer_8_out), .Q(register_2_q), .clk(ncs));  // open: en, clr
  assign buffer_9_out = buffer_3_out;  // Buffer buffer_9, 5 bits wide
  assign buffer_10_out = _3Y;  // Buffer buffer_10, 5 bits wide
  Shifter #(.width(32), .shift("lr")) shifter_1 (.in(32'h80000000), .\dist (register_1_q), .out(shifter_1_out));
  Register #(.width(5), .trigger("falling")) register_3 (
    .D(buffer_13_out), .Q(register_3_q), .clk(ncs));  // open: en, clr
  assign buffer_11_out = buffer_7_out;  // Buffer buffer_11, 5 bits wide
  assign buffer_12_out = buffer_11_out;  // Buffer buffer_12, 5 bits wide
  assign buffer_13_out = buffer_12_out;  // Buffer buffer_13, 5 bits wide
  Shifter #(.width(32), .shift("lr")) shifter_2 (.in(32'h80000000), .\dist (register_2_q), .out(shifter_2_out));
  Register #(.width(5), .trigger("falling")) register_4 (
    .D(buffer_16_out), .Q(register_4_q), .clk(ncs));  // open: en, clr
  assign buffer_14_out = buffer_15_out;  // Buffer buffer_14, 5 bits wide
  assign buffer_15_out = buffer_10_out;  // Buffer buffer_15, 5 bits wide
  assign buffer_16_out = buffer_14_out;  // Buffer buffer_16, 5 bits wide
  Demultiplexer #(.select(5), .width(32), .disabled(0), .enable("false")) demultiplexer_1 (
    .out0(_1_01), .out1(_1_02), .out2(_1_03), .out3(_1_04), .out4(_1_05), .out5(_1_06), .out6(_1_07),
    .out7(_1_08), .out8(_1_09), .out9(_1_10), .out10(_1_11), .out11(_1_12), .out12(_1_13), .out13(_1_14),
    .out14(_1_15), .out15(_1_16), .out16(_1_17), .out17(_1_18), .out18(_1_19), .out19(_1_20), .out20(_1_21),
    .out21(_1_22), .out22(_1_23), .out23(_1_24), .out24(_1_25), .out25(_1_26), .out26(_1_27), .out27(_1_28),
    .out28(_1_29), .out29(_1_30), .out30(_1_31), .out31(_1_32), .in(shifter_1_out), .sel(register_3_q));
  Demultiplexer #(.select(5), .width(32), .disabled(0), .enable("false")) demultiplexer_2 (
    .out0(_2_01), .out1(_2_02), .out2(_2_03), .out3(_2_04), .out4(_2_05), .out5(_2_06), .out6(_2_07),
    .out7(_2_08), .out8(_2_09), .out9(_2_10), .out10(_2_11), .out11(_2_12), .out12(_2_13), .out13(_2_14),
    .out14(_2_15), .out15(_2_16), .out16(_2_17), .out17(_2_18), .out18(_2_19), .out19(_2_20), .out20(_2_21),
    .out21(_2_22), .out22(_2_23), .out23(_2_24), .out24(_2_25), .out25(_2_26), .out26(_2_27), .out27(_2_28),
    .out28(_2_29), .out29(_2_30), .out30(_2_31), .out31(_2_32), .in(shifter_2_out), .sel(register_4_q));
  assign buffer_17_out = _4X;  // Buffer buffer_17, 5 bits wide
  assign buffer_18_out = _1X;  // Buffer buffer_18, 5 bits wide
  assign buffer_19_out = buffer_25_out;  // Buffer buffer_19, 5 bits wide
  assign buffer_20_out = buffer_17_out;  // Buffer buffer_20, 5 bits wide
  Register #(.width(5), .trigger("falling")) register_5 (
    .D(buffer_22_out), .Q(register_5_q), .clk(ncs));  // open: en, clr
  assign buffer_21_out = buffer_20_out;  // Buffer buffer_21, 5 bits wide
  assign buffer_22_out = buffer_21_out;  // Buffer buffer_22, 5 bits wide
  assign buffer_23_out = _4Y;  // Buffer buffer_23, 5 bits wide
  assign buffer_24_out = buffer_31_out;  // Buffer buffer_24, 5 bits wide
  assign buffer_25_out = buffer_18_out;  // Buffer buffer_25, 5 bits wide
  Register #(.width(5), .trigger("falling")) register_6 (
    .D(buffer_26_out), .Q(register_6_q), .clk(ncs));  // open: en, clr
  assign buffer_26_out = buffer_19_out;  // Buffer buffer_26, 5 bits wide
  assign buffer_27_out = _1Y;  // Buffer buffer_27, 5 bits wide
  assign buffer_28_out = buffer_27_out;  // Buffer buffer_28, 5 bits wide
  assign buffer_29_out = buffer_30_out;  // Buffer buffer_29, 5 bits wide
  assign buffer_30_out = buffer_28_out;  // Buffer buffer_30, 5 bits wide
  Shifter #(.width(32), .shift("lr")) shifter_3 (.in(32'h80000000), .\dist (register_5_q), .out(shifter_3_out));
  Demultiplexer #(.select(5), .width(32), .disabled(0), .enable("false")) demultiplexer_3 (
    .out0(_3_01), .out1(_3_02), .out2(_3_03), .out3(_3_04), .out4(_3_05), .out5(_3_06), .out6(_3_07),
    .out7(_3_08), .out8(_3_09), .out9(_3_10), .out10(_3_11), .out11(_3_12), .out12(_3_13), .out13(_3_14),
    .out14(_3_15), .out15(_3_16), .out16(_3_17), .out17(_3_18), .out18(_3_19), .out19(_3_20), .out20(_3_21),
    .out21(_3_22), .out22(_3_23), .out23(_3_24), .out24(_3_25), .out25(_3_26), .out26(_3_27), .out27(_3_28),
    .out28(_3_29), .out29(_3_30), .out30(_3_31), .out31(_3_32), .in(shifter_3_out), .sel(register_7_q));
  Register #(.width(5), .trigger("falling")) register_7 (
    .D(buffer_32_out), .Q(register_7_q), .clk(ncs));  // open: en, clr
  assign buffer_31_out = buffer_23_out;  // Buffer buffer_31, 5 bits wide
  assign buffer_32_out = buffer_24_out;  // Buffer buffer_32, 5 bits wide
  Demultiplexer #(.select(5), .width(32), .disabled(0), .enable("false")) demultiplexer_4 (
    .out0(_0_01), .out1(_0_02), .out2(_0_03), .out3(_0_04), .out4(_0_05), .out5(_0_06), .out6(_0_07),
    .out7(_0_08), .out8(_0_09), .out9(_0_10), .out10(_0_11), .out11(_0_12), .out12(_0_13), .out13(_0_14),
    .out14(_0_15), .out15(_0_16), .out16(_0_17), .out17(_0_18), .out18(_0_19), .out19(_0_20), .out20(_0_21),
    .out21(_0_22), .out22(_0_23), .out23(_0_24), .out24(_0_25), .out25(_0_26), .out26(_0_27), .out27(_0_28),
    .out28(_0_29), .out29(_0_30), .out30(_0_31), .out31(_0_32), .in(shifter_4_out), .sel(register_8_q));
  Shifter #(.width(32), .shift("lr")) shifter_4 (.in(32'h80000000), .\dist (register_6_q), .out(shifter_4_out));
  Register #(.width(5), .trigger("falling")) register_8 (
    .D(buffer_29_out), .Q(register_8_q), .clk(ncs));  // open: en, clr
endmodule
